// Logisim project pipeline processor.circ as structural Verilog: 23 circuits, main circuit pipelined_processor
module pipelined_processor (
  output zero_flag,
  output carry_out,
  output over_flow
);

  wire alu_op_0_id_ex, alu_op_0_if_id, alu_op_1_id_ex, alu_op_1_if_id, alu_op_2_id_ex, alu_op_2_if_id,
       alu_op_3_id_ex, alu_op_3_if_id, alu_op_4_id_ex, alu_op_4_if_id, alu_src_id_ex, alu_src_if_id,
       and_2_out, and_3_out, and_4_out, and_5_out, and_6_out, and_7_out, and_8_out, and_9_out, and_10_out,
       and_out, beq____success, beq_if_id, beq_neq_T_A, beqz_____success, beqz_if_id, bgez_____success,
       bgez_if_id, bgtz_____success, bgtz_if_id, blez_____success, blez_if_id, bltz_____success, bltz_if_id,
       bne____success, bne_if_id, bnez_____success, bnez_if_id, branch______taken, clk, comparator_2_eq,
       comparator_4_eq, comparator_4_gt, comparator_6_eq, comparator_6_lt, comparator_8_eq,
       five_extend_sel_id_ex, five_extend_sel_if_id, flush_if_reg, jal_ex_mem, jal_id_ex, jal_if_id,
       jalr_ex_mem, jalr_id_ex, jalr_if_id, jr_ex_mem, jr_id_ex, jr_if_id, jump_id_ex, jump_if_id,
       memory_read_ex_mem, memory_read_id_ex, memory_read_if_id, memory_to_register_ex_mem,
       memory_to_register_id_ex, memory_to_register_if_id, memory_write_ex_mem, memory_write_id_ex,
       memory_write_if_id, not_1_out, not_2_out, or_2_out, or_3_out, or_4_out, or_10_out, or_11_out,
       or_12_out, or_out, part__1__hazard, part__2__hazard, part__3__hazard, plus_jal_mem_wb,
       plus_jalr_mem_wb, plus_jr_mem_wb, plus_memory_read_mem_wb, plus_memory_to_register_mem_wb,
       plus_memory_write_mem_wb, plus_register_write_mem_wb, plus_set_mem_wb, plus_sset_mem_wb,
       register_write_ex_mem, register_write_id_ex, register_write_if_id, rest, set_ex_mem, set_id_ex,
       set_if_id, source_sel_1_id_ex, source_sel_1_if_id, source_sel_2_id_ex, source_sel_2_if_id,
       sset_ex_mem, sset_id_ex, sset_if_id, stall_id_ex_stop_pc, stall_support_1__5_extend_sel_id_ex,
       stall_support_1_alu_op_0_id_ex, stall_support_1_alu_op_1_id_ex, stall_support_1_alu_op_2_id_ex,
       stall_support_1_alu_op_3_id_ex, stall_support_1_alu_op_4_id_ex, stall_support_1_alu_src_id_ex,
       stall_support_1_jal_id_ex, stall_support_1_jalr_id_ex, stall_support_1_jr_id_ex,
       stall_support_1_jump_id_ex, stall_support_1_memory_read_id_ex,
       stall_support_1_memory_to_register_id_ex, stall_support_1_memory_write_id_ex,
       stall_support_1_reg_write_id_ex, stall_support_1_set_id_ex, stall_support_1_src_sel_1_id_ex,
       stall_support_1_src_sel_2_id_ex, stall_support_1_sset_id_ex, stall_support_1_swl_id_ex, sw_id_ex,
       sw_if_id, zero_B_T_A;
  wire [1:0] function_field_id_ex;
  wire [2:0] destination, destination_ex_mem, fwd_c, fwd_d, multiplexer_8_out, multiplexer_9_out,
       multiplexer_10_out, plus_destination_mem_wb, plus_rs_mem_wb, plus_rt_mem_wb, rd_id_ex, rs_ex_mem,
       rs_id_ex, rt_ex_mem, rt_id_ex;
  wire [3:0] fwd_a, fwd_b;
  wire [4:0] _5_bits_immediate_if_id, op_code_ex_mem, op_code_id_ex, op_code_if_id, plus_op_code_mem_wb;
  wire [7:0] _8_bits_immediate_id_ex;
  wire [7:5] _8_bits_immediate_if_id;
  wire [10:8] _11_bits_immediate_if_id;
  wire [15:0] multiplexer_5_out, rom_1_data;
  wire [17:0] address_lw_sw;
  wire [19:0] adder_1_out, bit_extender_1_out, pc, pc_1_ex_mem, pc_1_id_ex, pc_1_if_id;
  wire [31:0] _5_bits_immediate_extended_id_ex, _5_bits_immediate_extended_if_id,
       _5_bits_immediate_sign_entended_if_id, _8_bits_immediate_sign_extended_ex_mem,
       _8_bits_immediate_sign_extended_id_ex, _8_bits_immediate_sign_extended_if_id,
       _11_bits_immediate_sign_extended_id_ex, _11_bits_immediate_sign_extended_if_id, _32_bits_pc_1_if_id,
       alu_result_ex_mem, alu_result_for_sset, beq_bne_target_address_if_id, bit_extender_4_out,
       bit_extender_7_out, bus__1, bus__2, bus_a_if_id, bus_b_ex_mem, bus_b_id_ex, bus_b_if_id,
       jal____ex___mem, jal_jump_target_address_if_id, jr_jalr_target_address_if_id, memory_data,
       multiplexer_1_out, multiplexer_2_out, multiplexer_3_out, multiplexer_4_out, multiplexer_13_out,
       multiplexer_17_out, multiplexer_18_out, multiplexer_19_out, pc_1, pc_if_id,
       plus_8_bits_immediate_sign_extended_mem_wb, plus_alu_result_mem_wb, plus_data_in_reg_file,
       plus_memory_data_mem_wb, plus_pc_1_mem_wb, plus_sset_results_mem_wb, rd, rs, sset_results_ex_mem, x,
       y, zero_branches_target_address_if_id;

  Multiplexer #(.width(32), .enable("false")) multiplexer_1 (
    .in0(pc_1), .in1(zero_branches_target_address_if_id), .out(multiplexer_1_out), .sel(and_out));
  Multiplexer #(.width(32), .enable("false")) multiplexer_2 (
    .in0(multiplexer_1_out), .in1(beq_bne_target_address_if_id), .out(multiplexer_2_out), .sel(and_2_out));
  and \and  (and_out, zero_B_T_A, or_3_out);
  or \or  (or_out, jalr_if_id, jr_if_id);
  Multiplexer #(.width(32), .enable("false")) multiplexer_3 (
    .in0(multiplexer_2_out), .in1(jr_jalr_target_address_if_id), .out(multiplexer_3_out), .sel(or_out));
  Multiplexer #(.width(32), .enable("false")) multiplexer_4 (
    .in0(multiplexer_3_out), .in1(jal_jump_target_address_if_id), .out(multiplexer_4_out), .sel(or_2_out));
  and and_2 (and_2_out, or_4_out, beq_neq_T_A);
  or or_2 (or_2_out, jal_if_id, jump_if_id);
  Bit_Extender #(.in_width(32), .out_width(20)) bit_extender_1 (.in(multiplexer_4_out), .out(bit_extender_1_out));
  not not_1 (not_1_out, stall_id_ex_stop_pc);
  or or_3 (or_3_out, beqz_if_id, bltz_if_id, bgtz_if_id, bnez_if_id, bgez_if_id, blez_if_id);
  Counter #(.width(20), .max('hfffff)) u_PC (
    .load(not_1_out), .D(bit_extender_1_out), .count(1'b0), .Q(pc), .clk(clk), .clr(rest));  // open: carry
  Clock u_clk (.out(clk));
  or or_4 (or_4_out, bne_if_id, beq_if_id);
  Adder #(.width(20)) adder_1 (.a(pc), .b(20'h1), .out(adder_1_out), .cin(1'b0));  // open: cout
  assign pc_1 = {{12{1'b0}}, adder_1_out};  // Bit_Extender bit_extender_2
  ROM #(.addrWidth(20), .dataWidth(16)) rom_1 (.addr(pc), .data(rom_1_data), .sel(1'b1));
  Button u_rest (.out(rest));
  Multiplexer #(.width(16), .enable("false")) multiplexer_5 (
    .in0(rom_1_data), .in1(16'h1800), .out(multiplexer_5_out), .sel(flush_if_reg));
  IF_ID if_id_1 (
    ._20_bits_pc_1_TO_IF_ID(adder_1_out), ._16_bits_instruction_TO_IF_ID(multiplexer_5_out),
    ._20_bits_pc_1_ID_EX(pc_1_if_id),
    ._16_bits_instruction_to_ID_EX({op_code_if_id, _11_bits_immediate_if_id, _8_bits_immediate_if_id, _5_bits_immediate_if_id}),
    .EN(not_2_out), .CLK(clk), .REST(rest));
  not not_2 (not_2_out, stall_id_ex_stop_pc);
  assign _32_bits_pc_1_if_id = {{12{1'b0}}, pc_1_if_id};  // Bit_Extender bit_extender_3
  assign bit_extender_4_out = {{12{1'b0}}, pc_1_if_id};  // Bit_Extender bit_extender_4
  assign _11_bits_immediate_sign_extended_if_id = {{21{_11_bits_immediate_if_id[10]}}, {_11_bits_immediate_if_id, _8_bits_immediate_if_id, _5_bits_immediate_if_id}};  // Bit_Extender bit_extender_5
  assign _8_bits_immediate_sign_extended_if_id = {{24{_8_bits_immediate_if_id[7]}}, {_8_bits_immediate_if_id, _5_bits_immediate_if_id}};  // Bit_Extender bit_extender_6
  assign bit_extender_7_out = {{27{1'b0}}, _5_bits_immediate_if_id};  // Bit_Extender bit_extender_7
  assign _5_bits_immediate_sign_entended_if_id = {{27{_5_bits_immediate_if_id[4]}}, _5_bits_immediate_if_id};  // Bit_Extender bit_extender_8
  Subtractor #(.width(32)) subtractor_1 (.a(bit_extender_4_out), .b(32'h1), .out(pc_if_id));  // open: bin, bout
  Adder #(.width(32)) adder_2 (
    .a(pc_if_id), .b(_11_bits_immediate_sign_extended_if_id), .out(jal_jump_target_address_if_id));  // open: cin, cout
  Adder #(.width(32)) adder_3 (
    .a(pc_if_id), .b(_8_bits_immediate_sign_extended_if_id), .out(zero_branches_target_address_if_id));  // open: cin, cout
  Adder #(.width(32)) adder_4 (
    .a(pc_if_id), .b(_5_bits_immediate_sign_entended_if_id), .out(beq_bne_target_address_if_id));  // open: cin, cout
  Adder #(.width(32)) adder_5 (
    .a(_8_bits_immediate_sign_extended_if_id), .b(rd), .out(jr_jalr_target_address_if_id));  // open: cin, cout
  Comparator #(.width(32)) comparator_1 (.a(rd), .b({32{1'b0}}), .eq(beqz_____success));  // open: gt, lt
  Comparator #(.width(32)) comparator_2 (.a(rd), .b({32{1'b0}}), .eq(comparator_2_eq));  // open: gt, lt
  Comparator #(.width(32)) comparator_3 (.a(rd), .b({32{1'b0}}), .lt(bltz_____success));  // open: gt, eq
  Comparator #(.width(32)) comparator_4 (
    .a(rd), .b({32{1'b0}}), .gt(comparator_4_gt), .eq(comparator_4_eq));  // open: lt
  Comparator #(.width(32)) comparator_5 (.a(rd), .b({32{1'b0}}), .gt(bgtz_____success));  // open: eq, lt
  Comparator #(.width(32)) comparator_6 (
    .a(rd), .b({32{1'b0}}), .eq(comparator_6_eq), .lt(comparator_6_lt));  // open: gt
  Comparator #(.width(32)) comparator_7 (.a(rd), .b(rs), .eq(beq____success));  // open: gt, lt
  Comparator #(.width(32)) comparator_8 (.a(rd), .b(rs), .eq(comparator_8_eq));  // open: gt, lt
  not not_3 (bnez_____success, comparator_2_eq);
  or or_5 (bgez_____success, comparator_4_gt, comparator_4_eq);
  or or_6 (blez_____success, comparator_6_eq, comparator_6_lt);
  not not_4 (bne____success, comparator_8_eq);
  Multiplexer #(.width(32), .enable("false")) multiplexer_6 (
    .in0(bit_extender_7_out), .in1(_5_bits_immediate_sign_entended_if_id),
    .out(_5_bits_immediate_extended_if_id), .sel(five_extend_sel_if_id));
  control_unit control_unit_1 (
    .op_code(op_code_if_id), .source_sel_1(source_sel_1_if_id), .register_write(register_write_if_id),
    .memory_read(memory_read_if_id), .memory_write(memory_write_if_id),
    .memory_to_register(memory_to_register_if_id), .alu_src(alu_src_if_id), .alu_op_0(alu_op_0_if_id),
    .alu_op_1(alu_op_1_if_id), .alu_op_2(alu_op_2_if_id), .alu_op_3(alu_op_3_if_id),
    .alu_op_4(alu_op_4_if_id), .jump(jump_if_id), .jal(jal_if_id), .jr(jr_if_id), .jalr(jalr_if_id),
    .BEQ(beq_if_id), .BNE(bne_if_id), .BEQZ(beqz_if_id), .BNEZ(bnez_if_id), .BLTZ(bltz_if_id),
    .BGEZ(bgez_if_id), .BGTZ(bgtz_if_id), .BLEZ(blez_if_id), .SET(set_if_id), .SSET(sset_if_id),
    .source_sel_2(source_sel_2_if_id), .five_extend_sel(five_extend_sel_if_id), .SW(sw_if_id));
  or or_7 (beq_neq_T_A, and_3_out, and_4_out);
  or or_8 (branch______taken, and_3_out, and_4_out, and_5_out, and_6_out, and_7_out, and_8_out, and_9_out, and_10_out);
  or or_9 (zero_B_T_A, and_5_out, and_6_out, and_7_out, and_8_out, and_9_out, and_10_out);
  main_hazard_unit main_hazard_unit_1 (
    .hazard_unit_part_1(part__1__hazard), .hazard_unit_part_2(part__2__hazard),
    .hazard_unit_part_3(part__3__hazard), .branches_taken(branch______taken), .jr(jr_if_id),
    .jalr(jalr_if_id), .j(jump_if_id), .jal(jal_if_id), .stall_ID_EX__Disable_PC(stall_id_ex_stop_pc),
    .Stall_IF_ID(flush_if_reg));
  and and_3 (and_3_out, bne____success, bne_if_id);
  and and_4 (and_4_out, beq____success, beq_if_id);
  and and_5 (and_5_out, beqz_____success, beqz_if_id);
  and and_6 (and_6_out, bnez_____success, bnez_if_id);
  and and_7 (and_7_out, bltz_____success, bltz_if_id);
  and and_8 (and_8_out, bgez_____success, bgez_if_id);
  and and_9 (and_9_out, bgtz_____success, bgtz_if_id);
  and and_10 (and_10_out, blez_____success, blez_if_id);
  forwarding_unit_decoding_stage_d forwarding_unit_decoding_stage_d_1 (
    .op_code_ID_IF(op_code_if_id), .Rs_IF_ID(_8_bits_immediate_if_id), .RD_EX_MEM(destination_ex_mem),
    .op_code_EX_MEM(op_code_ex_mem), .op_code_EX_MEM_2(op_code_ex_mem), .op_code_EX_MEM_3(op_code_ex_mem),
    .register_write_EX_MEM(register_write_ex_mem), .sset_EX_MEM(sset_ex_mem), .set_EX_MEM(set_ex_mem),
    .memory_read_ex_mem(memory_read_ex_mem), .FWD_D(fwd_d));
  Multiplexer #(.select(3), .width(32), .enable("false")) multiplexer_7 (
    .in0(bus_b_if_id), .in1(alu_result_ex_mem), .in2(sset_results_ex_mem),
    .in3(_8_bits_immediate_sign_extended_ex_mem), .in4(jal____ex___mem), .in5(bus_b_if_id),
    .in6(bus_b_if_id), .in7(bus_b_if_id), .out(rs), .sel(fwd_d));
  Multiplexer #(.width(3), .enable("false")) multiplexer_8 (
    .in0(_5_bits_immediate_if_id[4:2]), .in1(_8_bits_immediate_if_id), .out(multiplexer_8_out),
    .sel(source_sel_1_if_id));
  Multiplexer #(.width(3), .enable("false")) multiplexer_9 (
    .in0(multiplexer_8_out), .in1(_11_bits_immediate_if_id), .out(multiplexer_9_out), .sel(source_sel_2_if_id));
  Multiplexer #(.width(3), .enable("false")) multiplexer_10 (
    .in0(_8_bits_immediate_if_id), .in1(_11_bits_immediate_if_id), .out(multiplexer_10_out), .sel(sw_if_id));
  Register_File register_file_1 (
    .Data_in(plus_data_in_reg_file), .BUS_A(bus_a_if_id), .BUS_B(bus_b_if_id),
    .Register_write(plus_register_write_mem_wb), .reg_destination(plus_destination_mem_wb), .CLK(clk),
    .REST(rest), .register_read_1(multiplexer_9_out), .register_read_2(multiplexer_10_out));
  forwarding_unit_decoding_stage_c forwarding_unit_decoding_stage_c_1 (
    .op_code_ID_IF(op_code_if_id), .op_code_ID_IF_2(op_code_if_id), .op_code_ID_IF_3(op_code_if_id),
    .RD_IF_ID(_11_bits_immediate_if_id), .RD_EX_MEM(destination_ex_mem), .op_code_EX_MEM(op_code_ex_mem),
    .op_code_EX_MEM_2(op_code_ex_mem), .op_code_EX_MEM_3(op_code_ex_mem),
    .register_write_EX_MEM(register_write_ex_mem), .sset_EX_MEM(sset_ex_mem), .set_EX_MEM(set_ex_mem),
    .memory_read_ex_mem(memory_read_ex_mem), .FWD_C(fwd_c));
  hazard_unit_part_1 hazard_unit_part_1_1 (
    .RD_IF_ID(_11_bits_immediate_if_id), .RS_IF_ID(_8_bits_immediate_if_id),
    .RT_IF_ID(_5_bits_immediate_if_id[4:2]), .RD_ID_EX(destination), .meory_read_ID_EX(memory_read_id_ex),
    .sset_IF_ID(sset_if_id), .op_code_IF_ID(op_code_if_id), .op_code_IF_ID_2(op_code_if_id),
    .stall_part_1(part__1__hazard));
  hazard_unit_part_2 hazard_unit_part_2_1 (
    .RS_IF_ID(_8_bits_immediate_if_id), .RD_EX_MEM(destination_ex_mem), .RD_IF_ID(_11_bits_immediate_if_id),
    .meory_read_EX_MEM(memory_read_ex_mem), .op_code_IF_ID(op_code_if_id), .op_code_IF_ID_2(op_code_if_id),
    .op_code_IF_ID_3(op_code_if_id), .RD_ID_EX(destination), .meory_read_ID_EX(memory_read_id_ex),
    .sset_ID_EX(sset_id_ex), .set_ID_EX(set_id_ex), .op_code_ID_EX(op_code_id_ex),
    .op_code_ID_EX_2(op_code_id_ex), .op_code_ID_EX_3(op_code_id_ex),
    .register_write_ID_EX(register_write_id_ex), .stall_part_2(part__2__hazard));
  hazard_unit_part_3 hazard_unit_part_3_1 (
    .RD_ID_EX(destination), .RD_EX_MEM(destination_ex_mem), .RD_IF_ID(_11_bits_immediate_if_id),
    .op_code_IF_ID(op_code_if_id), .register_write_EX_MEM(register_write_ex_mem),
    .register_write_ID_EX(register_write_id_ex), .stall_part_3(part__3__hazard));
  Multiplexer #(.select(3), .width(32), .enable("false")) multiplexer_11 (
    .in0(bus_a_if_id), .in1(alu_result_ex_mem), .in2(sset_results_ex_mem),
    .in3(_8_bits_immediate_sign_extended_ex_mem), .in4(jal____ex___mem), .in5(bus_a_if_id),
    .in6(bus_a_if_id), .in7(bus_a_if_id), .out(rd), .sel(fwd_c));
  stall_support stall_support_1 (
    .src_sel_1_IF_ID(source_sel_1_if_id), .jalr_IF_ID(jalr_if_id), .reg_write_IF_ID(register_write_if_id),
    .memory_read_IF_ID(memory_read_if_id), .memory_write_IF_ID(memory_write_if_id),
    .memory_to_register_IF_ID(memory_to_register_if_id), .alu_src_IF_ID(alu_src_if_id),
    .alu_op_0_IF_ID(alu_op_0_if_id), .alu_op_1_IF_ID(alu_op_1_if_id), .alu_op_2_IF_ID(alu_op_2_if_id),
    .alu_op_3_IF_ID(alu_op_3_if_id), .set_IF_ID(set_if_id), .alu_op_4_IF_ID(alu_op_4_if_id),
    .sset_IF_ID(sset_if_id), .jump_IF_ID(jump_if_id), .src_sel_2_IF_ID(source_sel_2_if_id),
    .jal_IF_ID(jal_if_id), ._5_extend_sel_IF_ID(five_extend_sel_if_id), .jr_IF_ID(jr_if_id),
    .sw_IF_ID(sw_if_id), .src_sel_1_ID_EX(stall_support_1_src_sel_1_id_ex),
    .jalr_ID_EX(stall_support_1_jalr_id_ex), .reg_write_ID_EX(stall_support_1_reg_write_id_ex),
    .memory_read_ID_EX(stall_support_1_memory_read_id_ex),
    .memory_write_ID_EX(stall_support_1_memory_write_id_ex),
    .memory_to_register_ID_EX(stall_support_1_memory_to_register_id_ex),
    .alu_src_ID_EX(stall_support_1_alu_src_id_ex), .alu_op_0_ID_EX(stall_support_1_alu_op_0_id_ex),
    .alu_op_1_ID_EX(stall_support_1_alu_op_1_id_ex), .alu_op_2_ID_EX(stall_support_1_alu_op_2_id_ex),
    .alu_op_3_ID_EX(stall_support_1_alu_op_3_id_ex), .set_ID_EX(stall_support_1_set_id_ex),
    .alu_op_4_ID_EX(stall_support_1_alu_op_4_id_ex), .sset_ID_EX(stall_support_1_sset_id_ex),
    .jump_ID_EX(stall_support_1_jump_id_ex), .src_sel_2_ID_EX(stall_support_1_src_sel_2_id_ex),
    .jal_ID_EX(stall_support_1_jal_id_ex), ._5_extend_sel_ID_EX(stall_support_1__5_extend_sel_id_ex),
    .jr_ID_EX(stall_support_1_jr_id_ex), .swl_ID_EX(stall_support_1_swl_id_ex), .stall(stall_id_ex_stop_pc));
  ID_EX id_ex_1 (
    ._20_PC_1_IF_ID(pc_1_if_id), .src_sel_1_IF_ID(stall_support_1_src_sel_1_id_ex),
    .jalr_IF_ID(stall_support_1_jalr_id_ex), .reg_write_IF_ID(stall_support_1_reg_write_id_ex),
    .memory_read_IF_ID(stall_support_1_memory_read_id_ex),
    .memory_write_IF_ID(stall_support_1_memory_write_id_ex),
    .memory_to_register_IF_ID(stall_support_1_memory_to_register_id_ex),
    .alu_src_IF_ID(stall_support_1_alu_src_id_ex), .alu_op_0_IF_ID(stall_support_1_alu_op_0_id_ex),
    .alu_op_1_IF_ID(stall_support_1_alu_op_1_id_ex), .alu_op_2_IF_ID(stall_support_1_alu_op_2_id_ex),
    .alu_op_3_IF_ID(stall_support_1_alu_op_3_id_ex), .set_IF_ID(stall_support_1_set_id_ex),
    .alu_op_4_IF_ID(stall_support_1_alu_op_4_id_ex), .sset_IF_ID(stall_support_1_sset_id_ex),
    .jump_IF_ID(stall_support_1_jump_id_ex), .src_sel_2_IF_ID(stall_support_1_src_sel_2_id_ex),
    .jal_IF_ID(stall_support_1_jal_id_ex), ._5_extend_sel_IF_ID(stall_support_1__5_extend_sel_id_ex),
    .jr_IF_ID(stall_support_1_jr_id_ex), .sw_IF_ID(stall_support_1_swl_id_ex),
    ._32_bits_src_A_IF_ID(bus_a_if_id), ._32_bits_src_B_IF_ID(bus_b_if_id),
    ._32_bits_5_extend_IF_ID(_5_bits_immediate_extended_if_id),
    ._32_bits_8_sign_extend_IF_ID(_8_bits_immediate_sign_extended_if_id),
    ._32_bits_11_sign_extend_IF_ID(_11_bits_immediate_sign_extended_if_id),
    ._3_bits_RT_IF_ID(_5_bits_immediate_if_id[4:2]), ._3_bits_RD_IF_ID(_11_bits_immediate_if_id),
    ._2_bits_FUNC_IF_ID(_5_bits_immediate_if_id[1:0]), ._20_PC_1_ID_EX(pc_1_id_ex),
    .src_sel_1_ID_EX(source_sel_1_id_ex), .jalr_ID_EX(jalr_id_ex), .reg_write_ID_EX(register_write_id_ex),
    .memory_read_ID_EX(memory_read_id_ex), .memory_write_ID_EX(memory_write_id_ex),
    .memory_to_register_ID_EX(memory_to_register_id_ex), .alu_src_ID_EX(alu_src_id_ex),
    .alu_op_0_ID_EX(alu_op_0_id_ex), .alu_op_1_ID_EX(alu_op_1_id_ex), .alu_op_2_ID_EX(alu_op_2_id_ex),
    .alu_op_3_ID_EX(alu_op_3_id_ex), .set_ID_EX(set_id_ex), .alu_op_4_ID_EX(alu_op_4_id_ex),
    .sset_ID_EX(sset_id_ex), .jump_ID_EX(jump_id_ex), .src_sel_2_ID_EX(source_sel_2_id_ex),
    .jal_ID_EX(jal_id_ex), ._5_extend_sel_ID_EX(five_extend_sel_id_ex), .jr_ID_EX(jr_id_ex),
    .swl_ID_EX(sw_id_ex), ._32_bits_src_A_ID_EX(bus__1), ._32_bits_src_B_ID_EX(bus_b_id_ex),
    ._32_bits_5_extend_ID_EX(_5_bits_immediate_extended_id_ex),
    ._32_bits_8_sign_extend_ID_EX(_8_bits_immediate_sign_extended_id_ex),
    ._32_bits_11_sign_extend_ID_EX(_11_bits_immediate_sign_extended_id_ex),
    ._8_bits_immediate_ID_EX(_8_bits_immediate_id_ex), ._3_bits_RS_ID_EX(rs_id_ex),
    ._3_bits_RT_ID_EX(rt_id_ex), ._3_bits_RD_ID_EX(rd_id_ex), ._2_bits_FUNC_ID_EX(function_field_id_ex),
    .CLK(clk), .REST(rest), ._5_bits_op_code_IF_ID(op_code_if_id), ._5_bits_op_code_ID_EX(op_code_id_ex),
    ._8_bits_immediate_IF_ID({_8_bits_immediate_if_id, _5_bits_immediate_if_id}),
    ._3_bits_RS_IF_ID(_8_bits_immediate_if_id), .EN(1'b1));
  Multiplexer #(.width(3), .enable("false")) multiplexer_12 (
    .in0(rd_id_ex), .in1(3'b111), .out(destination), .sel(or_10_out));
  or or_10 (or_10_out, jal_id_ex, jalr_id_ex);
  Multiplexer #(.width(32), .enable("false")) multiplexer_13 (
    .in0(bus_b_id_ex), .in1(_5_bits_immediate_extended_id_ex), .out(multiplexer_13_out), .sel(alu_src_id_ex));
  or or_11 (or_11_out, jal_id_ex, jalr_id_ex);
  Multiplexer #(.width(32), .enable("false")) multiplexer_14 (
    .in0(multiplexer_13_out), .in1(_8_bits_immediate_sign_extended_id_ex), .out(bus__2), .sel(or_11_out));
  Multiplexer #(.select(4), .width(32), .enable("false")) multiplexer_15 (
    .in0(bus__1), .in1(plus_memory_data_mem_wb), .in2(plus_alu_result_mem_wb),
    .in3(plus_sset_results_mem_wb), .in4(plus_8_bits_immediate_sign_extended_mem_wb), .in5(plus_pc_1_mem_wb),
    .in6(alu_result_ex_mem), .in7(sset_results_ex_mem), .in8(_8_bits_immediate_sign_extended_ex_mem),
    .in9(jal____ex___mem), .in10(bus__1), .in11(bus__1), .in12(bus__1), .in13(bus__1), .in14(bus__1),
    .in15(bus__1), .out(x), .sel(fwd_a));
  ALU alu_1 (
    .A(x), .B(y), .ALU_OP({alu_op_4_id_ex, alu_op_3_id_ex, alu_op_2_id_ex, alu_op_1_id_ex, alu_op_0_id_ex}),
    .fun(function_field_id_ex), .result(alu_result_for_sset), .zero_flag(zero_flag), .carry_out(carry_out),
    .over_flow(over_flow));  // open: branch
  forwarding_unit_execution_stage_a forwarding_unit_execution_stage_a_1 (
    .RD_MEM_WB(plus_destination_mem_wb), .RD_EX_MEM(destination_ex_mem), .RS_ID_EX(rs_id_ex),
    .RT_ID_EX(rt_id_ex), .RD_ID_EX(destination), .register_write_EX_MEM(register_write_ex_mem),
    .register_write_MEM_WB(plus_register_write_mem_wb), .sset_EX_MEM(sset_ex_mem), .sset_ID_EX(sset_id_ex),
    .set_EX_MEM(set_ex_mem), .memory_read_MEM_WB(plus_memory_read_mem_wb), .sset_MEM_WB(plus_sset_mem_wb),
    .set_MEM_WB(plus_set_mem_wb), .op_code_ID_EX(op_code_id_ex), .op_code_ID_EX_2(op_code_id_ex),
    .op_code_EX_MEM(op_code_ex_mem), .op_code_EX_MEM_2(op_code_ex_mem), .op_code_EX_MEM_3(op_code_ex_mem),
    .op_code_MEM_WB(plus_op_code_mem_wb), .op_code_MEM_WB_2(plus_op_code_mem_wb),
    .op_code_MEM_WB_3(plus_op_code_mem_wb), .memory_read_ex_mem(memory_read_ex_mem), .FWD_A(fwd_a));
  forwarding_unit_execution_stage_b forwarding_unit_execution_stage_b_1 (
    .RD_MEM_WB(plus_destination_mem_wb), .RD_EX_MEM(destination_ex_mem), .RS_ID_EX(rs_id_ex),
    .register_write_EX_MEM(register_write_ex_mem), .register_write_MEM_WB(plus_register_write_mem_wb),
    .sset_EX_MEM(sset_ex_mem), .set_EX_MEM(set_ex_mem), .memory_read_MEM_WB(plus_memory_read_mem_wb),
    .sset_MEM_WB(plus_sset_mem_wb), .set_MEM_WB(plus_set_mem_wb), .op_code_ID_EX(op_code_id_ex),
    .op_code_EX_MEM(op_code_ex_mem), .op_code_EX_MEM_2(op_code_ex_mem), .op_code_EX_MEM_3(op_code_ex_mem),
    .op_code_MEM_WB(plus_op_code_mem_wb), .op_code_MEM_WB_2(plus_op_code_mem_wb),
    .op_code_MEM_WB_3(plus_op_code_mem_wb), .memory_read_ex_mem(memory_read_ex_mem), .FWD_B(fwd_b));
  Multiplexer #(.select(4), .width(32), .enable("false")) multiplexer_16 (
    .in0(bus__2), .in1(plus_memory_data_mem_wb), .in2(plus_alu_result_mem_wb),
    .in3(plus_sset_results_mem_wb), .in4(plus_8_bits_immediate_sign_extended_mem_wb), .in5(plus_pc_1_mem_wb),
    .in6(alu_result_ex_mem), .in7(sset_results_ex_mem), .in8(_8_bits_immediate_sign_extended_ex_mem),
    .in9(jal____ex___mem), .in10(bus__2), .in11(bus__2), .in12(bus__2), .in13(bus__2), .in14(bus__2),
    .in15(bus__2), .out(y), .sel(fwd_b));
  EX_MEM ex_mem_1 (
    ._20_PC_1_ID_EX(pc_1_id_ex), .jalr_ID_EX(jalr_id_ex), .reg_write_ID_EX(register_write_id_ex),
    .memory_read_ID_EX(memory_read_id_ex), .memory_write_ID_EX(memory_write_id_ex),
    .memory_to_register_ID_EX(memory_to_register_id_ex), .set_ID_EX(set_id_ex), .sset_ID_EX(sset_id_ex),
    .jal_ID_EX(jal_id_ex), .jr_ID_EX(jr_id_ex), ._32_bits_sw_ID_EX(bus_b_id_ex),
    ._32_bits_result_ID_EX(alu_result_for_sset), ._3_bits_RT_ID_EX(rt_id_ex), ._3_bits_RD_ID_EX(destination),
    ._20_PC_1_EX_MEM(pc_1_ex_mem), .jalr_EX_MEM(jalr_ex_mem), .reg_write_EX_MEM(register_write_ex_mem),
    .memory_read_EX_MEM(memory_read_ex_mem), .memory_write_EX_MEM(memory_write_ex_mem),
    .memory_to_register_EX_MEM(memory_to_register_ex_mem), .set_EX_MEM(set_ex_mem),
    .sset_EX_MEM(sset_ex_mem), .jal_EX_MEM(jal_ex_mem), .jr_EX_MEM(jr_ex_mem),
    ._32_bits_sw_EX_MEM(bus_b_ex_mem), ._32_bits_results_EX_MEM(alu_result_ex_mem),
    ._3_bits_RS_EX_MEM(rs_ex_mem), ._3_bits_RT_EX_MEM(rt_ex_mem), ._3_bits_RD_EX_MEM(destination_ex_mem),
    .EN(1'b1), .CLK(clk), .REST(rest),
    ._32_bits_SSET_ID_EX({alu_result_for_sset[31:8], _8_bits_immediate_id_ex}),
    ._32_bits_SSET_EX_MEM(sset_results_ex_mem),
    ._8_bits_set_sign_ID_EX(_8_bits_immediate_sign_extended_id_ex),
    ._8_bits_set_sign_EX_MEM(_8_bits_immediate_sign_extended_ex_mem), ._5_bits_op_code_ID_EX(op_code_id_ex),
    ._5_bits_op_code_EX_MEM(op_code_ex_mem), ._3_bits_RS_ID_EX(rs_id_ex));
  assign jal____ex___mem = {{12{1'b0}}, pc_1_ex_mem};  // Bit_Extender bit_extender_9
  Bit_Extender #(.in_width(32), .out_width(18)) bit_extender_10 (.in(alu_result_ex_mem), .out(address_lw_sw));
  RAM #(.addrWidth(18), .dataWidth(32), .bus("separate")) ram_1 (
    .addr(address_lw_sw), .din(bus_b_ex_mem), .data(memory_data), .str(memory_write_ex_mem), .sel(1'b1),
    .clk(clk), .ld(memory_read_ex_mem), .clr(rest));
  MEM_WB mem_wb_1 (
    ._20_PC_1_EX_MEM(jal____ex___mem), .jalr_EX_MEM(jalr_ex_mem), .reg_write_EX_MEM(register_write_ex_mem),
    .memory_read_EX_MEM(memory_read_ex_mem), .memory_write_EX_MEM(memory_write_ex_mem),
    .memory_to_register_EX_MEM(memory_to_register_ex_mem), .set_EX_MEM(set_ex_mem),
    .sset_EX_MEM(sset_ex_mem), .jal_EX_MEM(jal_ex_mem), .jr_EX_MEM(jr_ex_mem),
    ._32_bits_MEM_EX_MEM(memory_data), ._32_bits_result_EX_MEM(alu_result_ex_mem),
    ._3_bits_RT_EX_MEM(rt_ex_mem), ._3_bits_RD_EX_MEM(destination_ex_mem),
    ._32_bits_SSET_EX_MEM(sset_results_ex_mem), ._20_PC_1_MEM_WB(plus_pc_1_mem_wb),
    .jalr_MEM_WB(plus_jalr_mem_wb), .reg_write_MEM_WB(plus_register_write_mem_wb),
    .memory_read_MEM_WB(plus_memory_read_mem_wb), .memory_write_MEM_WB(plus_memory_write_mem_wb),
    .memory_to_register_MEM_WB(plus_memory_to_register_mem_wb), .set_MEM_WB(plus_set_mem_wb),
    .sset_MEM_WB(plus_sset_mem_wb), .jal_MEM_WB(plus_jal_mem_wb), .jr_MEM_WB(plus_jr_mem_wb),
    ._32_bits_MEM_MEM_WB(plus_memory_data_mem_wb), ._32_bits_results_MEM_WB(plus_alu_result_mem_wb),
    ._3_bits_RS_MEM_WB(plus_rs_mem_wb), ._3_bits_RT_MEM_WB(plus_rt_mem_wb),
    ._3_bits_RD_MEM_WB(plus_destination_mem_wb), ._32_bits_SSET_MEM_WB(plus_sset_results_mem_wb), .EN(1'b1),
    .CLK(clk), .REST(rest), ._8_bits_set_sign_EX_MEM(_8_bits_immediate_sign_extended_ex_mem),
    ._8_bits_set_sign_MEM_WB(plus_8_bits_immediate_sign_extended_mem_wb),
    ._5_bits_op_code_EX_MEM(op_code_ex_mem), ._5_bits_op_code_MEM_WB(plus_op_code_mem_wb),
    ._3_bits_RS_EX_MEM(rs_ex_mem));
  Multiplexer #(.width(32), .enable("false")) multiplexer_17 (
    .in0(plus_alu_result_mem_wb), .in1(plus_memory_data_mem_wb), .out(multiplexer_17_out),
    .sel(plus_memory_to_register_mem_wb));
  Multiplexer #(.width(32), .enable("false")) multiplexer_18 (
    .in0(multiplexer_17_out), .in1(plus_8_bits_immediate_sign_extended_mem_wb), .out(multiplexer_18_out),
    .sel(plus_set_mem_wb));
  Multiplexer #(.width(32), .enable("false")) multiplexer_19 (
    .in0(multiplexer_18_out), .in1(plus_sset_results_mem_wb), .out(multiplexer_19_out), .sel(plus_sset_mem_wb));
  Multiplexer #(.width(32), .enable("false")) multiplexer_20 (
    .in0(multiplexer_19_out), .in1(plus_pc_1_mem_wb), .out(plus_data_in_reg_file), .sel(or_12_out));
  or or_12 (or_12_out, plus_jalr_mem_wb, plus_jal_mem_wb);

  // Other names for the same wires on the sheet: _8_bits_immediate_if_id[4:0] = _5_bits_immediate_if_id;
  //   _11_bits_immediate_if_id[7:0] = {_8_bits_immediate_if_id, _5_bits_immediate_if_id};
  //   function_field_if_id[1:0] = _5_bits_immediate_if_id[1:0]; rt_if_id[2:0] = _5_bits_immediate_if_id[4:2];
  //   rs_if_id[2:0] = _8_bits_immediate_if_id; rd_if_id[2:0] = _11_bits_immediate_if_id;
  //   alu_op_if_id[4:0] = {alu_op_4_if_id, alu_op_3_if_id, alu_op_2_if_id, alu_op_1_if_id, alu_op_0_if_id};
  //   alu_result_id_ex[31:0] = alu_result_for_sset; bus_a_id_ex[31:0] = bus__1;
  //   sset_results_id_ex[31:0] = {alu_result_for_sset[31:8], _8_bits_immediate_id_ex}

  // Notes on the sheet:
  //   next_pc
  //   pc+1
  //   instruction memory
  //   instruction fetch
  //   contents of rom_1 (hex, n*v repeats v):
  //   e155 e912 e910 e920 e900 e622 ee06 ee02 ee11 3c7 801 8100 8201 8302 448a c91 c50 d4e 7503 a28 701c
  //   8c00 f806 6ec8 8401 8502 ed4 701f 801 8100 8220 8321 44c 54d 8c01 8d02 d700
  //   pc+1_if/id
  //   16_bits_instruction
  //   pc
  //   control_unit
  //   instruction decoding
  //   main control hazards unit
  //   forwarding_unit_decoding_stage_d
  //   2:4
  //   5:7
  //   8:10
  //   mux_2
  //   source_sel_1
  //   source_sel_2
  //   sw
  //   control hazards units
  //   forwarding_unit_decoding_stage_c
  //   mux_1
  //   destenation_sel
  //   alu_src_mux_1
  //   alu_src
  //   alu_src_mux_2
  //   shifted_immediate
  //   mux_1
  //   intruction execution
  //   alu_result
  //   forwarding_unit_execution_stage_a
  //   forwarding_unit_execution_stage_b
  //   mux_2
  //   memory access
  //   data memory
  //   memory write back
  //   data _back_to_register_file
  //   memory_to_register
  //   set
  //   sset
  //   jal/jalr
endmodule

module control_unit (
  input  [4:0] op_code,
  output source_sel_1,
  output register_write,
  output memory_read,
  output memory_write,
  output memory_to_register,
  output alu_src,
  output alu_op_0,
  output alu_op_1,
  output alu_op_2,
  output alu_op_3,
  output alu_op_4,
  output jump,
  output jal,
  output jr,
  output jalr,
  output BEQ,
  output BNE,
  output BEQZ,
  output BNEZ,
  output BLTZ,
  output BGEZ,
  output BGTZ,
  output BLEZ,
  output SET,
  output SSET,
  output source_sel_2,
  output five_extend_sel,
  output SW
);

  Multiplexer #(.select(5), .width(28), .enable("false")) multiplexer_1 (
    .in0(28'h2), .in1(28'h42), .in2({28{1'b0}}), .in3({28{1'b0}}), .in4(28'ha3), .in5(28'he3), .in6(28'h123),
    .in7(28'h163), .in8(28'h40001a3), .in9(28'h40001e3), .in10(28'h4000223), .in11(28'h263), .in12(28'h2a3),
    .in13(28'h2e3), .in14(28'h6008300), .in15(28'h6010340), .in16(28'h40003b7), .in17(28'hc0003e9),
    .in18({28{1'b0}}), .in19({28{1'b0}}), .in20(28'h2020400), .in21(28'h2040440), .in22(28'h2080480),
    .in23(28'h21004c0), .in24(28'h2200500), .in25(28'h2400540), .in26(28'h2002580), .in27(28'h20045c2),
    .in28(28'h800002), .in29(28'h3000602), .in30(28'h800), .in31(28'h1002),
    .out({SW, five_extend_sel, source_sel_2, SSET, SET, BLEZ, BGTZ, BGEZ, BLTZ, BNEZ, BEQZ, BNE, BEQ, jalr, jr, jal, jump, alu_op_4, alu_op_3, alu_op_2, alu_op_1, alu_op_0, alu_src, memory_to_register, memory_write, memory_read, register_write, source_sel_1}),
    .sel(op_code));
endmodule

module ALU (
  input  [31:0] A,
  input  [31:0] B,
  input  [4:0] ALU_OP,
  input  [1:0] fun,
  output branch,
  output [31:0] result,
  output zero_flag,
  output carry_out,
  output over_flow
);

  wire and_2_out, and_3_out, bit_extender_14_out, bit_extender_15_out, carry_out_t, carry_out_t_t,
       comparator_1_lt, comparator_2_eq, comparator_3_eq, comparator_4_eq, comparator_5_eq, comparator_6_eq,
       comparator_7_lt, comparator_8_eq, comparator_8_gt, comparator_9_gt, comparator_10_eq,
       comparator_10_lt, multiplexer_3_out, multiplexer_4_out, not_1_out, not_2_out, or_2_out, or_3_out,
       xor_3_out, xor_4_out, xor_5_out, xor_6_out;
  wire [4:0] bit_extender_1_out, bit_extender_2_out, bit_extender_3_out;
  wire [31:0] and_out, bit_extender_4_out, bit_extender_5_out, bit_extender_6_out, bit_extender_7_out,
       bit_extender_8_out, bit_extender_9_out, bit_extender_10_out, bit_extender_11_out, bit_extender_12_out,
       bit_extender_13_out, multiplexer_1_out, multiplexer_2_out, or_out, shifter_1_out, shifter_2_out,
       shifter_3_out, shifter_4_out, tunnel, tunnel_t, xor_2_out, xor_out;

  Bit_Extender #(.in_width(32), .out_width(5)) bit_extender_1 (.in(B), .out(bit_extender_1_out));
  Bit_Extender #(.in_width(32), .out_width(5)) bit_extender_2 (.in(B), .out(bit_extender_2_out));
  Bit_Extender #(.in_width(32), .out_width(5)) bit_extender_3 (.in(B), .out(bit_extender_3_out));
  Adder #(.width(32)) adder_1 (.a(A), .b(B), .out(tunnel), .cin(1'b0), .cout(carry_out_t));
  Subtractor #(.width(32)) subtractor_1 (.a(B), .b(A), .out(tunnel_t), .bin(1'b0), .bout(carry_out_t_t));
  Comparator #(.width(32)) comparator_1 (.a(B), .b(A), .lt(comparator_1_lt));  // open: gt, eq
  Comparator #(.width(32)) comparator_2 (.a(A), .b(B), .eq(comparator_2_eq));  // open: gt, lt
  Shifter #(.width(32)) shifter_1 (.in(A), .\dist (bit_extender_1_out), .out(shifter_1_out));
  Shifter #(.width(32), .shift("lr")) shifter_2 (.in(A), .\dist (bit_extender_2_out), .out(shifter_2_out));
  Shifter #(.width(32), .shift("rl")) shifter_3 (.in(A), .\dist (bit_extender_3_out), .out(shifter_3_out));
  Comparator #(.width(32)) comparator_3 (.a(A), .b(B), .eq(comparator_3_eq));  // open: gt, lt
  Comparator #(.width(32)) comparator_4 (.a(A), .b(B), .eq(comparator_4_eq));  // open: gt, lt
  Comparator #(.width(32)) comparator_5 (.a(A), .b({32{1'b0}}), .eq(comparator_5_eq));  // open: gt, lt
  Comparator #(.width(32)) comparator_6 (.a(A), .b({32{1'b0}}), .eq(comparator_6_eq));  // open: gt, lt
  Comparator #(.width(32)) comparator_7 (.a(A), .b({32{1'b0}}), .lt(comparator_7_lt));  // open: gt, eq
  Comparator #(.width(32)) comparator_8 (
    .a(A), .b({32{1'b0}}), .gt(comparator_8_gt), .eq(comparator_8_eq));  // open: lt
  Comparator #(.width(32)) comparator_9 (.a(A), .b({32{1'b0}}), .gt(comparator_9_gt));  // open: eq, lt
  Comparator #(.width(32)) comparator_10 (
    .a(A), .b({32{1'b0}}), .eq(comparator_10_eq), .lt(comparator_10_lt));  // open: gt
  Shifter #(.width(32)) shifter_4 (.in(A), .\dist (5'b01000), .out(shifter_4_out));
  assign and_out = A & B;  // AND_Gate and, 32 bits wide
  assign or_out = A | B;  // OR_Gate or, 32 bits wide
  assign xor_out = A ^ B;  // XOR_Gate xor, 32 bits wide
  assign xor_2_out = ~A ^ B;  // XOR_Gate xor_2, 32 bits wide
  assign bit_extender_4_out = {{31{1'b0}}, comparator_3_eq};  // Bit_Extender bit_extender_4
  not not_1 (not_1_out, comparator_6_eq);
  or or_2 (or_2_out, comparator_8_gt, comparator_8_eq);
  assign bit_extender_5_out = {{31{1'b0}}, not_2_out};  // Bit_Extender bit_extender_5
  not not_2 (not_2_out, comparator_4_eq);
  assign bit_extender_6_out = {{31{1'b0}}, comparator_5_eq};  // Bit_Extender bit_extender_6
  assign bit_extender_7_out = {{31{1'b0}}, not_1_out};  // Bit_Extender bit_extender_7
  assign bit_extender_8_out = {{31{1'b0}}, comparator_7_lt};  // Bit_Extender bit_extender_8
  assign bit_extender_9_out = {{31{1'b0}}, comparator_9_gt};  // Bit_Extender bit_extender_9
  assign bit_extender_10_out = {{31{1'b0}}, or_3_out};  // Bit_Extender bit_extender_10
  or or_3 (or_3_out, comparator_10_eq, comparator_10_lt);
  assign bit_extender_11_out = {{31{1'b0}}, comparator_1_lt};  // Bit_Extender bit_extender_11
  assign bit_extender_12_out = {{31{1'b0}}, comparator_2_eq};  // Bit_Extender bit_extender_12
  assign bit_extender_13_out = {{31{1'b0}}, or_2_out};  // Bit_Extender bit_extender_13
  Multiplexer #(.select(2), .width(32), .enable("false")) multiplexer_1 (
    .in0(and_out), .in1(or_out), .in2(xor_out), .in3(xor_2_out), .out(multiplexer_1_out), .sel(fun));
  Multiplexer #(.select(2), .width(32), .enable("false")) multiplexer_2 (
    .in0(tunnel), .in1(tunnel_t), .in2(bit_extender_11_out), .in3(bit_extender_12_out),
    .out(multiplexer_2_out), .sel(fun));
  xor xor_3 (xor_3_out, A[31], tunnel[31]);
  xor xor_4 (xor_4_out, tunnel[31], B[31]);
  xor xor_5 (xor_5_out, A[31], tunnel_t[31]);
  xor xor_6 (xor_6_out, tunnel_t[31], ~B[31]);  // XOR_Gate
  and and_2 (and_2_out, xor_3_out, xor_4_out);
  and and_3 (and_3_out, xor_5_out, xor_6_out);
  Bit_Extender #(.in_width(2), .out_width(1)) bit_extender_14 (.in(fun), .out(bit_extender_14_out));
  Multiplexer #(.enable("false")) multiplexer_3 (
    .in0(carry_out_t), .in1(carry_out_t_t), .out(multiplexer_3_out), .sel(bit_extender_14_out));
  Bit_Extender #(.in_width(2), .out_width(1)) bit_extender_15 (.in(fun), .out(bit_extender_15_out));
  Multiplexer #(.enable("false")) multiplexer_4 (
    .in0(and_2_out), .in1(and_3_out), .out(multiplexer_4_out), .sel(bit_extender_15_out));
  Multiplexer #(.select(5), .width(32), .enable("false")) multiplexer_5 (
    .in0(multiplexer_1_out), .in1(multiplexer_2_out), .in2(and_out), .in3(or_out), .in4(xor_out),
    .in5(xor_2_out), .in6(tunnel), .in7(bit_extender_11_out), .in8(bit_extender_12_out), .in9(shifter_1_out),
    .in10(shifter_2_out), .in11(shifter_3_out), .in12(bit_extender_4_out), .in13(bit_extender_5_out),
    .in14(tunnel), .in15(tunnel), .in16(bit_extender_6_out), .in17(bit_extender_7_out),
    .in18(bit_extender_8_out), .in19(bit_extender_13_out), .in20(bit_extender_9_out),
    .in21(bit_extender_10_out), .in22(tunnel), .in23(tunnel), .in24(shifter_4_out), .in25({32{1'b0}}),
    .in26({32{1'b0}}), .in27({32{1'b0}}), .in28({32{1'b0}}), .in29({32{1'b0}}), .in30({32{1'b0}}),
    .in31({32{1'b0}}), .out({result[31:1], branch}), .sel(ALU_OP));
  Multiplexer #(.select(5), .enable("false")) multiplexer_6 (
    .in0(1'b0), .in1(multiplexer_3_out), .in2(1'b0), .in3(1'b0), .in4(1'b0), .in5(1'b0), .in6(carry_out_t),
    .in7(1'b0), .in8(1'b0), .in9(1'b0), .in10(1'b0), .in11(1'b0), .in12(1'b0), .in13(1'b0), .in14(1'b0),
    .in15(1'b0), .in16(1'b0), .in17(1'b0), .in18(1'b0), .in19(1'b0), .in20(1'b0), .in21(1'b0), .in22(1'b0),
    .in23(1'b0), .in24(1'b0), .in25(1'b0), .in26(1'b0), .in27(1'b0), .in28(1'b0), .in29(1'b0), .in30(1'b0),
    .in31(1'b0), .out(carry_out), .sel(ALU_OP));
  Multiplexer #(.select(5), .enable("false")) multiplexer_7 (
    .in0(1'b0), .in1(multiplexer_4_out), .in2(1'b0), .in3(1'b0), .in4(1'b0), .in5(1'b0), .in6(and_2_out),
    .in7(1'b0), .in8(1'b0), .in9(1'b0), .in10(1'b0), .in11(1'b0), .in12(1'b0), .in13(1'b0), .in14(1'b0),
    .in15(1'b0), .in16(1'b0), .in17(1'b0), .in18(1'b0), .in19(1'b0), .in20(1'b0), .in21(1'b0), .in22(1'b0),
    .in23(1'b0), .in24(1'b0), .in25(1'b0), .in26(1'b0), .in27(1'b0), .in28(1'b0), .in29(1'b0), .in30(1'b0),
    .in31(1'b0), .out(over_flow), .sel(ALU_OP));
  Comparator #(.width(32)) comparator_11 (.a({result[31:1], branch}), .b({32{1'b0}}), .eq(zero_flag));  // open: gt, lt

  assign result[0] = branch;

  // Notes on the sheet:
  //   slt
  //   seq
  //   sll
  //   srl
  //   ROR
endmodule

module Register_File (
  input  Register_write,
  input  [2:0] register_read_1,
  input  [2:0] register_read_2,
  input  [2:0] reg_destination,
  input  CLK,
  input  REST,
  input  [31:0] Data_in,
  output [31:0] BUS_A,
  output [31:0] BUS_B
);

  wire decoder_1_out0, decoder_1_out1, decoder_1_out2, decoder_1_out3, decoder_1_out4, decoder_1_out5,
       decoder_1_out6, decoder_1_out7;
  wire [31:0] R0_q, R1_q, R2_q, R3_q, R4_q, R5_q, R6_q, R7_q;

  Decoder #(.select(3), .disabled(0)) decoder_1 (
    .out0(decoder_1_out0), .out1(decoder_1_out1), .out2(decoder_1_out2), .out3(decoder_1_out3),
    .out4(decoder_1_out4), .out5(decoder_1_out5), .out6(decoder_1_out6), .out7(decoder_1_out7),
    .sel(reg_destination), .en(Register_write));
  Register #(.width(32), .trigger("high")) R0 (.D(Data_in), .en(decoder_1_out0), .Q(R0_q), .clk(CLK), .clr(REST));
  Register #(.width(32), .trigger("high")) R1 (.D(Data_in), .en(decoder_1_out1), .Q(R1_q), .clk(CLK), .clr(REST));
  Register #(.width(32), .trigger("high")) R2 (.D(Data_in), .en(decoder_1_out2), .Q(R2_q), .clk(CLK), .clr(REST));
  Register #(.width(32), .trigger("high")) R3 (.D(Data_in), .en(decoder_1_out3), .Q(R3_q), .clk(CLK), .clr(REST));
  Register #(.width(32), .trigger("high")) R4 (.D(Data_in), .en(decoder_1_out4), .Q(R4_q), .clk(CLK), .clr(REST));
  Register #(.width(32), .trigger("high")) R5 (.D(Data_in), .en(decoder_1_out5), .Q(R5_q), .clk(CLK), .clr(REST));
  Register #(.width(32), .trigger("high")) R6 (.D(Data_in), .en(decoder_1_out6), .Q(R6_q), .clk(CLK), .clr(REST));
  Register #(.width(32), .trigger("high")) R7 (.D(Data_in), .en(decoder_1_out7), .Q(R7_q), .clk(CLK), .clr(REST));
  Multiplexer #(.select(3), .width(32), .enable("false")) multiplexer_1 (
    .in0(R0_q), .in1(R1_q), .in2(R2_q), .in3(R3_q), .in4(R4_q), .in5(R5_q), .in6(R6_q), .in7(R7_q),
    .out(BUS_A), .sel(register_read_1));
  Multiplexer #(.select(3), .width(32), .enable("false")) multiplexer_2 (
    .in0(R0_q), .in1(R1_q), .in2(R2_q), .in3(R3_q), .in4(R4_q), .in5(R5_q), .in6(R6_q), .in7(R7_q),
    .out(BUS_B), .sel(register_read_2));
endmodule

module R_TYPE (
  input  [4:0] op_code,
  output r_type
);

  wire comparator_1_eq, comparator_2_eq;

  Comparator #(.width(5)) comparator_1 (.a(op_code), .b({5{1'b0}}), .eq(comparator_1_eq));  // open: gt, lt
  Comparator #(.width(5)) comparator_2 (.a(op_code), .b(5'b00001), .eq(comparator_2_eq));  // open: gt, lt
  or \or  (r_type, comparator_1_eq, comparator_2_eq);
endmodule

module I_TYPE (
  input  [4:0] op_code,
  output i_type
);

  wire comparator_1_eq, comparator_2_eq, comparator_3_eq, comparator_4_eq, comparator_5_eq, comparator_6_eq,
       comparator_7_eq, comparator_8_eq, comparator_9_eq, comparator_10_eq, comparator_11_eq,
       comparator_12_eq;

  Comparator #(.width(5)) comparator_1 (.a(op_code), .b(5'b00100), .eq(comparator_1_eq));  // open: gt, lt
  Comparator #(.width(5)) comparator_2 (.a(op_code), .b(5'b00101), .eq(comparator_2_eq));  // open: gt, lt
  Comparator #(.width(5)) comparator_3 (.a(op_code), .b(5'b00110), .eq(comparator_3_eq));  // open: gt, lt
  Comparator #(.width(5)) comparator_4 (.a(op_code), .b(5'b00111), .eq(comparator_4_eq));  // open: gt, lt
  Comparator #(.width(5)) comparator_5 (.a(op_code), .b(5'b01000), .eq(comparator_5_eq));  // open: gt, lt
  Comparator #(.width(5)) comparator_6 (.a(op_code), .b(5'b01001), .eq(comparator_6_eq));  // open: gt, lt
  Comparator #(.width(5)) comparator_7 (.a(op_code), .b(5'b01010), .eq(comparator_7_eq));  // open: gt, lt
  Comparator #(.width(5)) comparator_8 (.a(op_code), .b(5'b01011), .eq(comparator_8_eq));  // open: gt, lt
  Comparator #(.width(5)) comparator_9 (.a(op_code), .b(5'b01100), .eq(comparator_9_eq));  // open: gt, lt
  Comparator #(.width(5)) comparator_10 (.a(op_code), .b(5'b01101), .eq(comparator_10_eq));  // open: gt, lt
  Comparator #(.width(5)) comparator_11 (.a(op_code), .b(5'b10000), .eq(comparator_11_eq));  // open: gt, lt
  Comparator #(.width(5)) comparator_12 (.a(op_code), .b(5'b10001), .eq(comparator_12_eq));  // open: gt, lt
  or \or  (i_type, comparator_1_eq, comparator_2_eq, comparator_3_eq, comparator_4_eq, comparator_5_eq, comparator_6_eq, comparator_7_eq, comparator_8_eq, comparator_9_eq, comparator_10_eq, comparator_11_eq, comparator_12_eq);
endmodule

module JAL_JALR (
  input  [4:0] op_code,
  output jal_jalr
);

  wire comparator_1_eq, comparator_2_eq;

  Comparator #(.width(5)) comparator_1 (.a(op_code), .b(5'b11011), .eq(comparator_1_eq));  // open: gt, lt
  Comparator #(.width(5)) comparator_2 (.a(op_code), .b({5{1'b1}}), .eq(comparator_2_eq));  // open: gt, lt
  or \or  (jal_jalr, comparator_1_eq, comparator_2_eq);
endmodule

module beq_bne (
  input  [4:0] op_code,
  output beq_bne
);

  wire comparator_1_eq, comparator_2_eq;

  Comparator #(.width(5)) comparator_1 (.a(op_code), .b(5'b01111), .eq(comparator_1_eq));  // open: gt, lt
  Comparator #(.width(5)) comparator_2 (.a(op_code), .b(5'b01110), .eq(comparator_2_eq));  // open: gt, lt
  or \or  (beq_bne, comparator_1_eq, comparator_2_eq);
endmodule

module beranch_zero (
  input  [4:0] op_code,
  output branches_zeros
);

  wire comparator_1_eq, comparator_2_eq, comparator_3_eq, comparator_4_eq, comparator_5_eq, comparator_6_eq;

  Comparator #(.width(5)) comparator_1 (.a(op_code), .b(5'b10100), .eq(comparator_1_eq));  // open: gt, lt
  Comparator #(.width(5)) comparator_2 (.a(op_code), .b(5'b10101), .eq(comparator_2_eq));  // open: gt, lt
  Comparator #(.width(5)) comparator_3 (.a(op_code), .b(5'b10110), .eq(comparator_3_eq));  // open: gt, lt
  Comparator #(.width(5)) comparator_4 (.a(op_code), .b(5'b10111), .eq(comparator_4_eq));  // open: gt, lt
  Comparator #(.width(5)) comparator_5 (.a(op_code), .b(5'b11000), .eq(comparator_5_eq));  // open: gt, lt
  Comparator #(.width(5)) comparator_6 (.a(op_code), .b(5'b11001), .eq(comparator_6_eq));  // open: gt, lt
  or \or  (branches_zeros, comparator_1_eq, comparator_2_eq, comparator_3_eq, comparator_4_eq, comparator_5_eq, comparator_6_eq);
endmodule

module jr_jalr (
  input  [4:0] op_code,
  output jr_jalr
);

  wire comparator_1_eq, comparator_2_eq;

  Comparator #(.width(5)) comparator_1 (.a(op_code), .b(5'b11011), .eq(comparator_1_eq));  // open: gt, lt
  Comparator #(.width(5)) comparator_2 (.a(op_code), .b(5'b11010), .eq(comparator_2_eq));  // open: gt, lt
  or \or  (jr_jalr, comparator_1_eq, comparator_2_eq);
endmodule

module IF_ID (
  input  EN,
  input  [19:0] _20_bits_pc_1_TO_IF_ID,
  input  [15:0] _16_bits_instruction_TO_IF_ID,
  input  CLK,
  input  REST,
  output [19:0] _20_bits_pc_1_ID_EX,
  output [15:0] _16_bits_instruction_to_ID_EX
);

  Register #(.width(20)) register_1 (
    .D(_20_bits_pc_1_TO_IF_ID), .en(EN), .Q(_20_bits_pc_1_ID_EX), .clk(CLK), .clr(REST));
  Register #(.width(16)) register_2 (
    .D(_16_bits_instruction_TO_IF_ID), .en(EN), .Q(_16_bits_instruction_to_ID_EX), .clk(CLK), .clr(REST));
endmodule

module ID_EX (
  input  EN,
  input  [4:0] _5_bits_op_code_IF_ID,
  input  [19:0] _20_PC_1_IF_ID,
  input  src_sel_1_IF_ID,
  input  jalr_IF_ID,
  input  reg_write_IF_ID,
  input  memory_read_IF_ID,
  input  memory_write_IF_ID,
  input  memory_to_register_IF_ID,
  input  alu_src_IF_ID,
  input  alu_op_0_IF_ID,
  input  alu_op_1_IF_ID,
  input  alu_op_2_IF_ID,
  input  alu_op_3_IF_ID,
  input  set_IF_ID,
  input  alu_op_4_IF_ID,
  input  sset_IF_ID,
  input  jump_IF_ID,
  input  src_sel_2_IF_ID,
  input  jal_IF_ID,
  input  _5_extend_sel_IF_ID,
  input  jr_IF_ID,
  input  sw_IF_ID,
  input  [31:0] _32_bits_src_A_IF_ID,
  input  [31:0] _32_bits_src_B_IF_ID,
  input  [31:0] _32_bits_5_extend_IF_ID,
  input  [31:0] _32_bits_8_sign_extend_IF_ID,
  input  [31:0] _32_bits_11_sign_extend_IF_ID,
  input  [7:0] _8_bits_immediate_IF_ID,
  input  [2:0] _3_bits_RS_IF_ID,
  input  [2:0] _3_bits_RT_IF_ID,
  input  [2:0] _3_bits_RD_IF_ID,
  input  [1:0] _2_bits_FUNC_IF_ID,
  input  REST,
  input  CLK,
  output [4:0] _5_bits_op_code_ID_EX,
  output [19:0] _20_PC_1_ID_EX,
  output src_sel_1_ID_EX,
  output jalr_ID_EX,
  output reg_write_ID_EX,
  output memory_read_ID_EX,
  output memory_write_ID_EX,
  output memory_to_register_ID_EX,
  output alu_src_ID_EX,
  output alu_op_0_ID_EX,
  output alu_op_1_ID_EX,
  output alu_op_2_ID_EX,
  output alu_op_3_ID_EX,
  output set_ID_EX,
  output alu_op_4_ID_EX,
  output sset_ID_EX,
  output jump_ID_EX,
  output src_sel_2_ID_EX,
  output jal_ID_EX,
  output _5_extend_sel_ID_EX,
  output jr_ID_EX,
  output swl_ID_EX,
  output [31:0] _32_bits_src_A_ID_EX,
  output [31:0] _32_bits_src_B_ID_EX,
  output [31:0] _32_bits_5_extend_ID_EX,
  output [31:0] _32_bits_8_sign_extend_ID_EX,
  output [31:0] _32_bits_11_sign_extend_ID_EX,
  output [7:0] _8_bits_immediate_ID_EX,
  output [2:0] _3_bits_RS_ID_EX,
  output [2:0] _3_bits_RT_ID_EX,
  output [2:0] _3_bits_RD_ID_EX,
  output [1:0] _2_bits_FUNC_ID_EX
);

  Register #(.width(5)) register_1 (
    .D(_5_bits_op_code_IF_ID), .en(EN), .Q(_5_bits_op_code_ID_EX), .clk(CLK), .clr(REST));
  Register #(.width(20)) register_2 (.D(_20_PC_1_IF_ID), .en(EN), .Q(_20_PC_1_ID_EX), .clk(CLK), .clr(REST));
  Register #(.width(1)) register_3 (.D(src_sel_1_IF_ID), .en(EN), .Q(src_sel_1_ID_EX), .clk(CLK), .clr(REST));
  Register #(.width(1)) register_4 (.D(reg_write_IF_ID), .en(EN), .Q(reg_write_ID_EX), .clk(CLK), .clr(REST));
  Register #(.width(1)) register_5 (.D(memory_read_IF_ID), .en(EN), .Q(memory_read_ID_EX), .clk(CLK), .clr(REST));
  Register #(.width(1)) register_6 (.D(memory_write_IF_ID), .en(EN), .Q(memory_write_ID_EX), .clk(CLK), .clr(REST));
  Register #(.width(1)) register_7 (
    .D(memory_to_register_IF_ID), .en(EN), .Q(memory_to_register_ID_EX), .clk(CLK), .clr(REST));
  Register #(.width(1)) register_8 (.D(alu_src_IF_ID), .en(EN), .Q(alu_src_ID_EX), .clk(CLK), .clr(REST));
  Register #(.width(1)) register_9 (.D(alu_op_0_IF_ID), .en(EN), .Q(alu_op_0_ID_EX), .clk(CLK), .clr(REST));
  Register #(.width(1)) register_10 (.D(alu_op_1_IF_ID), .en(EN), .Q(alu_op_1_ID_EX), .clk(CLK), .clr(REST));
  Register #(.width(1)) register_11 (.D(alu_op_2_IF_ID), .en(EN), .Q(alu_op_2_ID_EX), .clk(CLK), .clr(REST));
  Register #(.width(1)) register_12 (.D(alu_op_3_IF_ID), .en(EN), .Q(alu_op_3_ID_EX), .clk(CLK), .clr(REST));
  Register #(.width(1)) register_13 (.D(alu_op_4_IF_ID), .en(EN), .Q(alu_op_4_ID_EX), .clk(CLK), .clr(REST));
  Register #(.width(1)) register_14 (.D(jump_IF_ID), .en(EN), .Q(jump_ID_EX), .clk(CLK), .clr(REST));
  Register #(.width(1)) register_15 (.D(jal_IF_ID), .en(EN), .Q(jal_ID_EX), .clk(CLK), .clr(REST));
  Register #(.width(1)) register_16 (.D(jr_IF_ID), .en(EN), .Q(jr_ID_EX), .clk(CLK), .clr(REST));
  Register #(.width(32)) register_17 (
    .D(_32_bits_src_A_IF_ID), .en(EN), .Q(_32_bits_src_A_ID_EX), .clk(CLK), .clr(REST));
  Register #(.width(32)) register_18 (
    .D(_32_bits_src_B_IF_ID), .en(EN), .Q(_32_bits_src_B_ID_EX), .clk(CLK), .clr(REST));
  Register #(.width(32)) register_19 (
    .D(_32_bits_5_extend_IF_ID), .en(EN), .Q(_32_bits_5_extend_ID_EX), .clk(CLK), .clr(REST));
  Register #(.width(32)) register_20 (
    .D(_32_bits_8_sign_extend_IF_ID), .en(EN), .Q(_32_bits_8_sign_extend_ID_EX), .clk(CLK), .clr(REST));
  Register #(.width(32)) register_21 (
    .D(_32_bits_11_sign_extend_IF_ID), .en(EN), .Q(_32_bits_11_sign_extend_ID_EX), .clk(CLK), .clr(REST));
  Register register_22 (.D(_8_bits_immediate_IF_ID), .en(EN), .Q(_8_bits_immediate_ID_EX), .clk(CLK), .clr(REST));
  Register #(.width(3)) register_23 (.D(_3_bits_RS_IF_ID), .en(EN), .Q(_3_bits_RS_ID_EX), .clk(CLK), .clr(REST));
  Register #(.width(3)) register_24 (.D(_3_bits_RT_IF_ID), .en(EN), .Q(_3_bits_RT_ID_EX), .clk(CLK), .clr(REST));
  Register #(.width(3)) register_25 (.D(_3_bits_RD_IF_ID), .en(EN), .Q(_3_bits_RD_ID_EX), .clk(CLK), .clr(REST));
  Register #(.width(2)) register_26 (.D(_2_bits_FUNC_IF_ID), .en(EN), .Q(_2_bits_FUNC_ID_EX), .clk(CLK), .clr(REST));
  Register #(.width(1)) register_27 (.D(jalr_IF_ID), .en(EN), .Q(jalr_ID_EX), .clk(CLK), .clr(REST));
  Register #(.width(1)) register_28 (.D(set_IF_ID), .en(EN), .Q(set_ID_EX), .clk(CLK), .clr(REST));
  Register #(.width(1)) register_29 (.D(sset_IF_ID), .en(EN), .Q(sset_ID_EX), .clk(CLK), .clr(REST));
  Register #(.width(1)) register_30 (.D(src_sel_2_IF_ID), .en(EN), .Q(src_sel_2_ID_EX), .clk(CLK), .clr(REST));
  Register #(.width(1)) register_31 (.D(_5_extend_sel_IF_ID), .en(EN), .Q(_5_extend_sel_ID_EX), .clk(CLK), .clr(REST));
  Register #(.width(1)) register_32 (.D(sw_IF_ID), .en(EN), .Q(swl_ID_EX), .clk(CLK), .clr(REST));
endmodule

module EX_MEM (
  input  EN,
  input  [4:0] _5_bits_op_code_ID_EX,
  input  [31:0] _8_bits_set_sign_ID_EX,
  input  [19:0] _20_PC_1_ID_EX,
  input  jalr_ID_EX,
  input  reg_write_ID_EX,
  input  memory_read_ID_EX,
  input  memory_write_ID_EX,
  input  memory_to_register_ID_EX,
  input  set_ID_EX,
  input  sset_ID_EX,
  input  jal_ID_EX,
  input  jr_ID_EX,
  input  [31:0] _32_bits_sw_ID_EX,
  input  [31:0] _32_bits_result_ID_EX,
  input  [2:0] _3_bits_RS_ID_EX,
  input  [2:0] _3_bits_RT_ID_EX,
  input  [2:0] _3_bits_RD_ID_EX,
  input  [31:0] _32_bits_SSET_ID_EX,
  input  REST,
  input  CLK,
  output [4:0] _5_bits_op_code_EX_MEM,
  output [31:0] _8_bits_set_sign_EX_MEM,
  output [19:0] _20_PC_1_EX_MEM,
  output jalr_EX_MEM,
  output reg_write_EX_MEM,
  output memory_read_EX_MEM,
  output memory_write_EX_MEM,
  output memory_to_register_EX_MEM,
  output set_EX_MEM,
  output sset_EX_MEM,
  output jal_EX_MEM,
  output jr_EX_MEM,
  output [31:0] _32_bits_sw_EX_MEM,
  output [31:0] _32_bits_results_EX_MEM,
  output [2:0] _3_bits_RS_EX_MEM,
  output [2:0] _3_bits_RT_EX_MEM,
  output [2:0] _3_bits_RD_EX_MEM,
  output [31:0] _32_bits_SSET_EX_MEM
);

  Register #(.width(5)) register_1 (
    .D(_5_bits_op_code_ID_EX), .en(EN), .Q(_5_bits_op_code_EX_MEM), .clk(CLK), .clr(REST));
  Register #(.width(32)) register_2 (
    .D(_8_bits_set_sign_ID_EX), .en(EN), .Q(_8_bits_set_sign_EX_MEM), .clk(CLK), .clr(REST));
  Register #(.width(20)) register_3 (.D(_20_PC_1_ID_EX), .en(EN), .Q(_20_PC_1_EX_MEM), .clk(CLK), .clr(REST));
  Register #(.width(1)) register_4 (.D(reg_write_ID_EX), .en(EN), .Q(reg_write_EX_MEM), .clk(CLK), .clr(REST));
  Register #(.width(1)) register_5 (.D(memory_read_ID_EX), .en(EN), .Q(memory_read_EX_MEM), .clk(CLK), .clr(REST));
  Register #(.width(1)) register_6 (.D(memory_write_ID_EX), .en(EN), .Q(memory_write_EX_MEM), .clk(CLK), .clr(REST));
  Register #(.width(1)) register_7 (
    .D(memory_to_register_ID_EX), .en(EN), .Q(memory_to_register_EX_MEM), .clk(CLK), .clr(REST));
  Register #(.width(1)) register_8 (.D(jal_ID_EX), .en(EN), .Q(jal_EX_MEM), .clk(CLK), .clr(REST));
  Register #(.width(1)) register_9 (.D(jr_ID_EX), .en(EN), .Q(jr_EX_MEM), .clk(CLK), .clr(REST));
  Register #(.width(32)) register_10 (.D(_32_bits_sw_ID_EX), .en(EN), .Q(_32_bits_sw_EX_MEM), .clk(CLK), .clr(REST));
  Register #(.width(32)) register_11 (
    .D(_32_bits_result_ID_EX), .en(EN), .Q(_32_bits_results_EX_MEM), .clk(CLK), .clr(REST));
  Register #(.width(3)) register_12 (.D(_3_bits_RS_ID_EX), .en(EN), .Q(_3_bits_RS_EX_MEM), .clk(CLK), .clr(REST));
  Register #(.width(3)) register_13 (.D(_3_bits_RT_ID_EX), .en(EN), .Q(_3_bits_RT_EX_MEM), .clk(CLK), .clr(REST));
  Register #(.width(3)) register_14 (.D(_3_bits_RD_ID_EX), .en(EN), .Q(_3_bits_RD_EX_MEM), .clk(CLK), .clr(REST));
  Register #(.width(32)) register_15 (
    .D(_32_bits_SSET_ID_EX), .en(EN), .Q(_32_bits_SSET_EX_MEM), .clk(CLK), .clr(REST));
  Register #(.width(1)) register_16 (.D(jalr_ID_EX), .en(EN), .Q(jalr_EX_MEM), .clk(CLK), .clr(REST));
  Register #(.width(1)) register_17 (.D(set_ID_EX), .en(EN), .Q(set_EX_MEM), .clk(CLK), .clr(REST));
  Register #(.width(1)) register_18 (.D(sset_ID_EX), .en(EN), .Q(sset_EX_MEM), .clk(CLK), .clr(REST));
endmodule

module MEM_WB (
  input  EN,
  input  [4:0] _5_bits_op_code_EX_MEM,
  input  [31:0] _8_bits_set_sign_EX_MEM,
  input  [31:0] _20_PC_1_EX_MEM,
  input  jalr_EX_MEM,
  input  reg_write_EX_MEM,
  input  memory_read_EX_MEM,
  input  memory_write_EX_MEM,
  input  memory_to_register_EX_MEM,
  input  set_EX_MEM,
  input  sset_EX_MEM,
  input  jal_EX_MEM,
  input  jr_EX_MEM,
  input  [31:0] _32_bits_MEM_EX_MEM,
  input  [31:0] _32_bits_result_EX_MEM,
  input  [2:0] _3_bits_RS_EX_MEM,
  input  [2:0] _3_bits_RT_EX_MEM,
  input  [2:0] _3_bits_RD_EX_MEM,
  input  [31:0] _32_bits_SSET_EX_MEM,
  input  REST,
  input  CLK,
  output [4:0] _5_bits_op_code_MEM_WB,
  output [31:0] _8_bits_set_sign_MEM_WB,
  output [31:0] _20_PC_1_MEM_WB,
  output jalr_MEM_WB,
  output reg_write_MEM_WB,
  output memory_read_MEM_WB,
  output memory_write_MEM_WB,
  output memory_to_register_MEM_WB,
  output set_MEM_WB,
  output sset_MEM_WB,
  output jal_MEM_WB,
  output jr_MEM_WB,
  output [31:0] _32_bits_MEM_MEM_WB,
  output [31:0] _32_bits_results_MEM_WB,
  output [2:0] _3_bits_RS_MEM_WB,
  output [2:0] _3_bits_RT_MEM_WB,
  output [2:0] _3_bits_RD_MEM_WB,
  output [31:0] _32_bits_SSET_MEM_WB
);

  Register #(.width(5)) register_1 (
    .D(_5_bits_op_code_EX_MEM), .en(EN), .Q(_5_bits_op_code_MEM_WB), .clk(CLK), .clr(REST));
  Register #(.width(32)) register_2 (
    .D(_8_bits_set_sign_EX_MEM), .en(EN), .Q(_8_bits_set_sign_MEM_WB), .clk(CLK), .clr(REST));
  Register #(.width(32)) register_3 (.D(_20_PC_1_EX_MEM), .en(EN), .Q(_20_PC_1_MEM_WB), .clk(CLK), .clr(REST));
  Register #(.width(1)) register_4 (.D(reg_write_EX_MEM), .en(EN), .Q(reg_write_MEM_WB), .clk(CLK), .clr(REST));
  Register #(.width(1)) register_5 (.D(memory_read_EX_MEM), .en(EN), .Q(memory_read_MEM_WB), .clk(CLK), .clr(REST));
  Register #(.width(1)) register_6 (.D(memory_write_EX_MEM), .en(EN), .Q(memory_write_MEM_WB), .clk(CLK), .clr(REST));
  Register #(.width(1)) register_7 (
    .D(memory_to_register_EX_MEM), .en(EN), .Q(memory_to_register_MEM_WB), .clk(CLK), .clr(REST));
  Register #(.width(1)) register_8 (.D(jal_EX_MEM), .en(EN), .Q(jal_MEM_WB), .clk(CLK), .clr(REST));
  Register #(.width(1)) register_9 (.D(jr_EX_MEM), .en(EN), .Q(jr_MEM_WB), .clk(CLK), .clr(REST));
  Register #(.width(32)) register_10 (.D(_32_bits_MEM_EX_MEM), .en(EN), .Q(_32_bits_MEM_MEM_WB), .clk(CLK), .clr(REST));
  Register #(.width(32)) register_11 (
    .D(_32_bits_result_EX_MEM), .en(EN), .Q(_32_bits_results_MEM_WB), .clk(CLK), .clr(REST));
  Register #(.width(3)) register_12 (.D(_3_bits_RS_EX_MEM), .en(EN), .Q(_3_bits_RS_MEM_WB), .clk(CLK), .clr(REST));
  Register #(.width(3)) register_13 (.D(_3_bits_RT_EX_MEM), .en(EN), .Q(_3_bits_RT_MEM_WB), .clk(CLK), .clr(REST));
  Register #(.width(3)) register_14 (.D(_3_bits_RD_EX_MEM), .en(EN), .Q(_3_bits_RD_MEM_WB), .clk(CLK), .clr(REST));
  Register #(.width(32)) register_15 (
    .D(_32_bits_SSET_EX_MEM), .en(EN), .Q(_32_bits_SSET_MEM_WB), .clk(CLK), .clr(REST));
  Register #(.width(1)) register_16 (.D(jalr_EX_MEM), .en(EN), .Q(jalr_MEM_WB), .clk(CLK), .clr(REST));
  Register #(.width(1)) register_17 (.D(set_EX_MEM), .en(EN), .Q(set_MEM_WB), .clk(CLK), .clr(REST));
  Register #(.width(1)) register_18 (.D(sset_EX_MEM), .en(EN), .Q(sset_MEM_WB), .clk(CLK), .clr(REST));
endmodule

module forwarding_unit_execution_stage_a (
  input  [2:0] RD_MEM_WB,
  input  [2:0] RD_EX_MEM,
  input  [2:0] RS_ID_EX,
  input  [2:0] RT_ID_EX,
  input  [2:0] RD_ID_EX,
  input  register_write_EX_MEM,
  input  register_write_MEM_WB,
  input  sset_EX_MEM,
  input  sset_ID_EX,
  input  set_EX_MEM,
  input  memory_read_MEM_WB,
  input  sset_MEM_WB,
  input  set_MEM_WB,
  input  [4:0] op_code_ID_EX,
  input  [4:0] op_code_ID_EX_2,
  input  [4:0] op_code_EX_MEM,
  input  [4:0] op_code_EX_MEM_2,
  input  [4:0] op_code_EX_MEM_3,
  input  [4:0] op_code_MEM_WB,
  input  [4:0] op_code_MEM_WB_2,
  input  [4:0] op_code_MEM_WB_3,
  input  memory_read_ex_mem,
  output [3:0] FWD_A
);

  wire alu_res_execution, alu_res_memory, and_2_out, and_3_out, and_4_out, and_5_out, and_6_out, and_7_out,
       and_8_out, and_9_out, and_10_out, and_11_out, and_12_out, and_17_out, and_18_out, and_19_out,
       and_20_out, and_21_out, and_22_out, and_23_out, and_24_out, and_25_out, and_26_out, and_27_out,
       and_28_out, and_29_out, and_30_out, and_31_out, and_out, comparator_1_eq, comparator_2_eq,
       comparator_3_eq, comparator_4_eq, comparator_5_eq, comparator_6_eq, comparator_7_eq, comparator_8_eq,
       comparator_9_eq, comparator_10_eq, comparator_11_eq, comparator_12_eq, comparator_13_eq,
       comparator_14_eq, comparator_15_eq, comparator_16_eq, comparator_17_eq, comparator_18_eq,
       comparator_19_eq, comparator_20_eq, comparator_21_eq, comparator_22_eq, comparator_23_eq,
       comparator_24_eq, comparator_25_eq, comparator_26_eq, comparator_27_eq, I_TYPE, I_TYPE_EX_MEM,
       I_TYPE_MEM_WB, jal_jalr_EX_MEM, jal_jalr_execution, jal_jalr_MEM_WB, jal_jalr_memory, lw_fwd,
       not_1_out, not_2_out, not_3_out, not_4_out, not_5_out, not_6_out, not_7_out, not_8_out, not_9_out,
       or_3_out, or_4_out, or_5_out, or_6_out, or_7_out, or_8_out, or_9_out, or_10_out, or_11_out,
       R_I_TYPE_EX_MEM, R_I_TYPE_MEM_WB, R_TYPE, R_TYPE_EX_MEM, R_TYPE_MRM_WB, set_execution, set_memory,
       sset_execution, sset_memory;
  wire [3:0] multiplexer_1_out, multiplexer_2_out, multiplexer_3_out, multiplexer_4_out, multiplexer_5_out,
       multiplexer_6_out, multiplexer_7_out, multiplexer_8_out;

  R_TYPE r_type_1 (.op_code(op_code_ID_EX), .r_type(R_TYPE));
  I_TYPE i_type_1 (.op_code(op_code_ID_EX_2), .i_type(I_TYPE));
  JAL_JALR jal_jalr_1 (.op_code(op_code_EX_MEM), .jal_jalr(jal_jalr_EX_MEM));
  R_TYPE r_type_2 (.op_code(op_code_EX_MEM_2), .r_type(R_TYPE_EX_MEM));
  I_TYPE i_type_2 (.op_code(op_code_EX_MEM_3), .i_type(I_TYPE_EX_MEM));
  R_TYPE r_type_3 (.op_code(op_code_MEM_WB), .r_type(R_TYPE_MRM_WB));
  I_TYPE i_type_3 (.op_code(op_code_MEM_WB_2), .i_type(I_TYPE_MEM_WB));
  JAL_JALR jal_jalr_2 (.op_code(op_code_MEM_WB_3), .jal_jalr(jal_jalr_MEM_WB));
  or \or  (R_I_TYPE_EX_MEM, R_TYPE_EX_MEM, I_TYPE_EX_MEM);
  or or_2 (R_I_TYPE_MEM_WB, R_TYPE_MRM_WB, I_TYPE_MEM_WB);
  Comparator #(.width(3)) comparator_1 (.a(RD_ID_EX), .b(RD_EX_MEM), .eq(comparator_1_eq));  // open: gt, lt
  Comparator #(.width(3)) comparator_2 (.a(RT_ID_EX), .b(RD_EX_MEM), .eq(comparator_2_eq));  // open: gt, lt
  Comparator #(.width(3)) comparator_3 (.a(RS_ID_EX), .b(RD_EX_MEM), .eq(comparator_3_eq));  // open: gt, lt
  Comparator #(.width(3)) comparator_4 (.a(RD_ID_EX), .b(RD_MEM_WB), .eq(comparator_4_eq));  // open: gt, lt
  Comparator #(.width(3)) comparator_5 (.a(RT_ID_EX), .b(RD_MEM_WB), .eq(comparator_5_eq));  // open: gt, lt
  Comparator #(.width(3)) comparator_6 (.a(RS_ID_EX), .b(RD_MEM_WB), .eq(comparator_6_eq));  // open: gt, lt
  Comparator #(.width(3)) comparator_7 (.a(RD_ID_EX), .b(RD_EX_MEM), .eq(comparator_7_eq));  // open: gt, lt
  Comparator #(.width(3)) comparator_8 (.a(RT_ID_EX), .b(RD_EX_MEM), .eq(comparator_8_eq));  // open: gt, lt
  Comparator #(.width(3)) comparator_9 (.a(RS_ID_EX), .b(RD_EX_MEM), .eq(comparator_9_eq));  // open: gt, lt
  Comparator #(.width(3)) comparator_10 (.a(RD_ID_EX), .b(RD_MEM_WB), .eq(comparator_10_eq));  // open: gt, lt
  Comparator #(.width(3)) comparator_11 (.a(RT_ID_EX), .b(RD_MEM_WB), .eq(comparator_11_eq));  // open: gt, lt
  Comparator #(.width(3)) comparator_12 (.a(RS_ID_EX), .b(RD_MEM_WB), .eq(comparator_12_eq));  // open: gt, lt
  and \and  (and_out, sset_ID_EX, comparator_1_eq);
  and and_2 (and_2_out, R_TYPE, comparator_2_eq);
  and and_3 (and_3_out, I_TYPE, comparator_3_eq);
  and and_4 (and_4_out, sset_ID_EX, comparator_4_eq);
  and and_5 (and_5_out, R_TYPE, comparator_5_eq);
  and and_6 (and_6_out, I_TYPE, comparator_6_eq);
  and and_7 (and_7_out, sset_ID_EX, comparator_7_eq);
  and and_8 (and_8_out, R_TYPE, comparator_8_eq);
  and and_9 (and_9_out, I_TYPE, comparator_9_eq);
  and and_10 (and_10_out, sset_ID_EX, comparator_10_eq);
  and and_11 (and_11_out, R_TYPE, comparator_11_eq);
  and and_12 (and_12_out, I_TYPE, comparator_12_eq);
  or or_3 (or_3_out, and_out, and_2_out, and_3_out);
  or or_4 (or_4_out, and_4_out, and_5_out, and_6_out);
  or or_5 (or_5_out, and_7_out, and_8_out, and_9_out);
  or or_6 (or_6_out, and_10_out, and_11_out, and_12_out);
  not not_1 (not_1_out, memory_read_ex_mem);
  not not_2 (not_2_out, register_write_EX_MEM);
  not not_3 (not_3_out, memory_read_MEM_WB);
  not not_4 (not_4_out, register_write_EX_MEM);
  not not_5 (not_5_out, memory_read_MEM_WB);
  and and_13 (alu_res_execution, not_1_out, or_3_out, register_write_EX_MEM, R_I_TYPE_EX_MEM);
  and and_14 (alu_res_memory, not_2_out, register_write_MEM_WB, or_4_out, not_3_out, R_I_TYPE_MEM_WB);
  and and_15 (set_execution, set_EX_MEM, or_5_out, register_write_EX_MEM);
  and and_16 (set_memory, not_4_out, set_MEM_WB, or_6_out, not_5_out);
  Comparator #(.width(3)) comparator_13 (.a(RD_ID_EX), .b(RD_MEM_WB), .eq(comparator_13_eq));  // open: gt, lt
  Comparator #(.width(3)) comparator_14 (.a(RT_ID_EX), .b(RD_MEM_WB), .eq(comparator_14_eq));  // open: gt, lt
  Comparator #(.width(3)) comparator_15 (.a(RS_ID_EX), .b(RD_MEM_WB), .eq(comparator_15_eq));  // open: gt, lt
  and and_17 (and_17_out, sset_ID_EX, comparator_13_eq);
  and and_18 (and_18_out, R_TYPE, comparator_14_eq);
  and and_19 (and_19_out, I_TYPE, comparator_15_eq);
  or or_7 (or_7_out, and_17_out, and_18_out, and_19_out);
  Comparator #(.width(3)) comparator_16 (.a(RT_ID_EX), .b(RD_EX_MEM), .eq(comparator_16_eq));  // open: gt, lt
  Comparator #(.width(3)) comparator_17 (.a(RS_ID_EX), .b(RD_EX_MEM), .eq(comparator_17_eq));  // open: gt, lt
  Comparator #(.width(3)) comparator_18 (.a(RD_ID_EX), .b(RD_MEM_WB), .eq(comparator_18_eq));  // open: gt, lt
  Comparator #(.width(3)) comparator_19 (.a(RT_ID_EX), .b(RD_MEM_WB), .eq(comparator_19_eq));  // open: gt, lt
  Comparator #(.width(3)) comparator_20 (.a(RS_ID_EX), .b(RD_MEM_WB), .eq(comparator_20_eq));  // open: gt, lt
  Comparator #(.width(3)) comparator_21 (.a(RD_ID_EX), .b(3'b111), .eq(comparator_21_eq));  // open: gt, lt
  Comparator #(.width(3)) comparator_22 (.a(RT_ID_EX), .b(3'b111), .eq(comparator_22_eq));  // open: gt, lt
  Comparator #(.width(3)) comparator_23 (.a(RS_ID_EX), .b(3'b111), .eq(comparator_23_eq));  // open: gt, lt
  Comparator #(.width(3)) comparator_24 (.a(RD_ID_EX), .b(3'b111), .eq(comparator_24_eq));  // open: gt, lt
  Comparator #(.width(3)) comparator_25 (.a(RT_ID_EX), .b(3'b111), .eq(comparator_25_eq));  // open: gt, lt
  Comparator #(.width(3)) comparator_26 (.a(RS_ID_EX), .b(3'b111), .eq(comparator_26_eq));  // open: gt, lt
  Comparator #(.width(3)) comparator_27 (.a(RD_ID_EX), .b(RD_EX_MEM), .eq(comparator_27_eq));  // open: gt, lt
  and and_20 (and_20_out, sset_ID_EX, comparator_21_eq);
  and and_21 (and_21_out, R_TYPE, comparator_22_eq);
  and and_22 (and_22_out, I_TYPE, comparator_23_eq);
  and and_23 (and_23_out, sset_ID_EX, comparator_24_eq);
  not not_6 (not_6_out, register_write_EX_MEM);
  and and_24 (and_24_out, sset_ID_EX, comparator_27_eq);
  and and_25 (and_25_out, R_TYPE, comparator_16_eq);
  and and_26 (and_26_out, I_TYPE, comparator_17_eq);
  and and_27 (and_27_out, sset_ID_EX, comparator_18_eq);
  and and_28 (and_28_out, R_TYPE, comparator_19_eq);
  and and_29 (and_29_out, I_TYPE, comparator_20_eq);
  and and_30 (and_30_out, R_TYPE, comparator_25_eq);
  and and_31 (and_31_out, I_TYPE, comparator_26_eq);
  and and_32 (lw_fwd, register_write_MEM_WB, or_7_out, memory_read_MEM_WB, not_6_out);
  or or_8 (or_8_out, and_24_out, and_25_out, and_26_out);
  or or_9 (or_9_out, and_27_out, and_28_out, and_29_out);
  or or_10 (or_10_out, and_20_out, and_21_out, and_22_out);
  or or_11 (or_11_out, and_23_out, and_30_out, and_31_out);
  not not_7 (not_7_out, register_write_EX_MEM);
  not not_8 (not_8_out, memory_read_MEM_WB);
  and and_33 (jal_jalr_execution, jal_jalr_EX_MEM, or_10_out, register_write_EX_MEM);
  and and_34 (jal_jalr_memory, register_write_MEM_WB, or_11_out, jal_jalr_MEM_WB, not_9_out);
  not not_9 (not_9_out, register_write_EX_MEM);
  and and_35 (sset_execution, sset_EX_MEM, or_8_out, register_write_EX_MEM);
  and and_36 (sset_memory, not_7_out, sset_MEM_WB, or_9_out, not_8_out);
  Multiplexer #(.width(4), .enable("false")) multiplexer_1 (
    .in0(4'b0000), .in1(4'b0001), .out(multiplexer_1_out), .sel(lw_fwd));
  Multiplexer #(.width(4), .enable("false")) multiplexer_2 (
    .in0(multiplexer_1_out), .in1(4'b0010), .out(multiplexer_2_out), .sel(alu_res_memory));
  Multiplexer #(.width(4), .enable("false")) multiplexer_3 (
    .in0(multiplexer_2_out), .in1(4'b0011), .out(multiplexer_3_out), .sel(sset_memory));
  Multiplexer #(.width(4), .enable("false")) multiplexer_4 (
    .in0(multiplexer_3_out), .in1(4'b0100), .out(multiplexer_4_out), .sel(set_memory));
  Multiplexer #(.width(4), .enable("false")) multiplexer_5 (
    .in0(multiplexer_4_out), .in1(4'b0101), .out(multiplexer_5_out), .sel(jal_jalr_memory));
  Multiplexer #(.width(4), .enable("false")) multiplexer_6 (
    .in0(multiplexer_5_out), .in1(4'b0110), .out(multiplexer_6_out), .sel(alu_res_execution));
  Multiplexer #(.width(4), .enable("false")) multiplexer_7 (
    .in0(multiplexer_6_out), .in1(4'b0111), .out(multiplexer_7_out), .sel(sset_execution));
  Multiplexer #(.width(4), .enable("false")) multiplexer_8 (
    .in0(multiplexer_7_out), .in1(4'b1000), .out(multiplexer_8_out), .sel(set_execution));
  Multiplexer #(.width(4), .enable("false")) multiplexer_9 (
    .in0(multiplexer_8_out), .in1(4'b1001), .out(FWD_A), .sel(jal_jalr_execution));
endmodule

module forwarding_unit_execution_stage_b (
  input  [2:0] RD_MEM_WB,
  input  [2:0] RD_EX_MEM,
  input  [2:0] RS_ID_EX,
  input  register_write_EX_MEM,
  input  register_write_MEM_WB,
  input  sset_EX_MEM,
  input  set_EX_MEM,
  input  memory_read_MEM_WB,
  input  sset_MEM_WB,
  input  set_MEM_WB,
  input  [4:0] op_code_ID_EX,
  input  [4:0] op_code_EX_MEM,
  input  [4:0] op_code_EX_MEM_2,
  input  [4:0] op_code_EX_MEM_3,
  input  [4:0] op_code_MEM_WB,
  input  [4:0] op_code_MEM_WB_2,
  input  [4:0] op_code_MEM_WB_3,
  input  memory_read_ex_mem,
  output [3:0] FWD_B
);

  wire alu_res_execution, alu_res_memory, and_2_out, and_3_out, and_4_out, and_5_out, and_6_out, and_7_out,
       and_8_out, and_9_out, and_out, comparator_1_eq, comparator_2_eq, comparator_3_eq, comparator_4_eq,
       comparator_5_eq, comparator_6_eq, comparator_7_eq, comparator_8_eq, comparator_9_eq, I_TYPE_EX_MEM,
       I_TYPE_MEM_WB, jal_jalr_EX_MEM, jal_jalr_execution, jal_jalr_MEM_WB, jal_jalr_memory, lw_fwd,
       not_1_out, not_2_out, not_3_out, not_4_out, not_5_out, not_6_out, not_7_out, not_8_out, not_9_out,
       R_I_TYPE_EX_MEM, R_I_TYPE_MEM_WB, R_TYPE, R_TYPE_EX_MEM, R_TYPE_MRM_WB, set_execution, set_memory,
       sset_execution, sset_memory;
  wire [3:0] multiplexer_1_out, multiplexer_2_out, multiplexer_3_out, multiplexer_4_out, multiplexer_5_out,
       multiplexer_6_out, multiplexer_7_out, multiplexer_8_out;

  R_TYPE r_type_1 (.op_code(op_code_ID_EX), .r_type(R_TYPE));
  JAL_JALR jal_jalr_1 (.op_code(op_code_EX_MEM), .jal_jalr(jal_jalr_EX_MEM));
  R_TYPE r_type_2 (.op_code(op_code_EX_MEM_2), .r_type(R_TYPE_EX_MEM));
  I_TYPE i_type_1 (.op_code(op_code_EX_MEM_3), .i_type(I_TYPE_EX_MEM));
  R_TYPE r_type_3 (.op_code(op_code_MEM_WB), .r_type(R_TYPE_MRM_WB));
  I_TYPE i_type_2 (.op_code(op_code_MEM_WB_2), .i_type(I_TYPE_MEM_WB));
  JAL_JALR jal_jalr_2 (.op_code(op_code_MEM_WB_3), .jal_jalr(jal_jalr_MEM_WB));
  or \or  (R_I_TYPE_EX_MEM, R_TYPE_EX_MEM, I_TYPE_EX_MEM);
  or or_2 (R_I_TYPE_MEM_WB, R_TYPE_MRM_WB, I_TYPE_MEM_WB);
  Comparator #(.width(3)) comparator_1 (.a(RS_ID_EX), .b(3'b111), .eq(comparator_1_eq));  // open: gt, lt
  Comparator #(.width(3)) comparator_2 (.a(RS_ID_EX), .b(3'b111), .eq(comparator_2_eq));  // open: gt, lt
  Comparator #(.width(3)) comparator_3 (.a(RS_ID_EX), .b(RD_MEM_WB), .eq(comparator_3_eq));  // open: gt, lt
  Comparator #(.width(3)) comparator_4 (.a(RS_ID_EX), .b(RD_EX_MEM), .eq(comparator_4_eq));  // open: gt, lt
  Comparator #(.width(3)) comparator_5 (.a(RS_ID_EX), .b(RD_EX_MEM), .eq(comparator_5_eq));  // open: gt, lt
  Comparator #(.width(3)) comparator_6 (.a(RS_ID_EX), .b(RD_MEM_WB), .eq(comparator_6_eq));  // open: gt, lt
  Comparator #(.width(3)) comparator_7 (.a(RS_ID_EX), .b(RD_EX_MEM), .eq(comparator_7_eq));  // open: gt, lt
  Comparator #(.width(3)) comparator_8 (.a(RS_ID_EX), .b(RD_MEM_WB), .eq(comparator_8_eq));  // open: gt, lt
  Comparator #(.width(3)) comparator_9 (.a(RS_ID_EX), .b(RD_MEM_WB), .eq(comparator_9_eq));  // open: gt, lt
  and \and  (and_out, R_TYPE, comparator_5_eq);
  and and_2 (and_2_out, R_TYPE, comparator_6_eq);
  and and_3 (and_3_out, R_TYPE, comparator_7_eq);
  and and_4 (and_4_out, R_TYPE, comparator_8_eq);
  and and_5 (and_5_out, R_TYPE, comparator_9_eq);
  and and_6 (and_6_out, R_TYPE, comparator_1_eq);
  and and_7 (and_7_out, R_TYPE, comparator_2_eq);
  and and_8 (and_8_out, R_TYPE, comparator_3_eq);
  and and_9 (and_9_out, R_TYPE, comparator_4_eq);
  not not_1 (not_1_out, memory_read_ex_mem);
  not not_2 (not_2_out, register_write_EX_MEM);
  not not_3 (not_3_out, memory_read_MEM_WB);
  not not_4 (not_4_out, register_write_EX_MEM);
  not not_5 (not_5_out, memory_read_MEM_WB);
  not not_6 (not_6_out, register_write_EX_MEM);
  not not_7 (not_7_out, register_write_EX_MEM);
  and and_10 (alu_res_execution, not_1_out, and_out, register_write_EX_MEM, R_I_TYPE_EX_MEM);
  and and_11 (alu_res_memory, not_2_out, register_write_MEM_WB, and_2_out, not_3_out, R_I_TYPE_MEM_WB);
  and and_12 (set_execution, set_EX_MEM, and_3_out, register_write_EX_MEM);
  and and_13 (set_memory, not_4_out, set_MEM_WB, and_4_out, not_5_out);
  and and_14 (lw_fwd, register_write_MEM_WB, and_5_out, memory_read_MEM_WB, not_6_out);
  and and_15 (jal_jalr_memory, register_write_MEM_WB, and_6_out, jal_jalr_MEM_WB, not_7_out);
  and and_16 (jal_jalr_execution, jal_jalr_EX_MEM, and_7_out, register_write_EX_MEM);
  not not_8 (not_8_out, register_write_EX_MEM);
  and and_17 (sset_memory, not_8_out, sset_MEM_WB, and_8_out, not_9_out);
  not not_9 (not_9_out, memory_read_MEM_WB);
  and and_18 (sset_execution, sset_EX_MEM, and_9_out, register_write_EX_MEM);
  Multiplexer #(.width(4), .enable("false")) multiplexer_1 (
    .in0(4'b0000), .in1(4'b0001), .out(multiplexer_1_out), .sel(lw_fwd));
  Multiplexer #(.width(4), .enable("false")) multiplexer_2 (
    .in0(multiplexer_1_out), .in1(4'b0010), .out(multiplexer_2_out), .sel(alu_res_memory));
  Multiplexer #(.width(4), .enable("false")) multiplexer_3 (
    .in0(multiplexer_2_out), .in1(4'b0011), .out(multiplexer_3_out), .sel(sset_memory));
  Multiplexer #(.width(4), .enable("false")) multiplexer_4 (
    .in0(multiplexer_3_out), .in1(4'b0100), .out(multiplexer_4_out), .sel(set_memory));
  Multiplexer #(.width(4), .enable("false")) multiplexer_5 (
    .in0(multiplexer_4_out), .in1(4'b0101), .out(multiplexer_5_out), .sel(jal_jalr_memory));
  Multiplexer #(.width(4), .enable("false")) multiplexer_6 (
    .in0(multiplexer_5_out), .in1(4'b0110), .out(multiplexer_6_out), .sel(alu_res_execution));
  Multiplexer #(.width(4), .enable("false")) multiplexer_7 (
    .in0(multiplexer_6_out), .in1(4'b0111), .out(multiplexer_7_out), .sel(sset_execution));
  Multiplexer #(.width(4), .enable("false")) multiplexer_8 (
    .in0(multiplexer_7_out), .in1(4'b1000), .out(multiplexer_8_out), .sel(set_execution));
  Multiplexer #(.width(4), .enable("false")) multiplexer_9 (
    .in0(multiplexer_8_out), .in1(4'b1001), .out(FWD_B), .sel(jal_jalr_execution));
endmodule

module forwarding_unit_decoding_stage_c (
  input  [4:0] op_code_ID_IF,
  input  [4:0] op_code_ID_IF_2,
  input  [4:0] op_code_ID_IF_3,
  input  [2:0] RD_IF_ID,
  input  [2:0] RD_EX_MEM,
  input  [4:0] op_code_EX_MEM,
  input  [4:0] op_code_EX_MEM_2,
  input  [4:0] op_code_EX_MEM_3,
  input  register_write_EX_MEM,
  input  sset_EX_MEM,
  input  set_EX_MEM,
  input  memory_read_ex_mem,
  output [2:0] FWD_C
);

  wire alu_res_execution, and_2_out, and_3_out, and_4_out, and_5_out, and_6_out, and_7_out, and_8_out,
       and_9_out, and_10_out, and_11_out, and_12_out, and_out, beq_bneif_id, branches_zero_if_id,
       comparator_1_eq, comparator_2_eq, comparator_3_eq, comparator_4_eq, comparator_5_eq, comparator_6_eq,
       comparator_7_eq, comparator_8_eq, comparator_9_eq, comparator_10_eq, comparator_11_eq,
       comparator_12_eq, I_TYPE_EX_MEM, jal_jalr_ex_mem, jal_jalr_execution, jr_jalr_if_id, not_1_out,
       or_2_out, or_3_out, or_4_out, or_5_out, R_I_TYPE_EX_MEM, R_TYPE_EX_MEM, set_execution, sset_execution;
  wire [2:0] multiplexer_1_out, multiplexer_2_out, multiplexer_3_out;

  beq_bne beq_bne_1 (.op_code(op_code_ID_IF), .beq_bne(beq_bneif_id));
  beranch_zero beranch_zero_1 (.op_code(op_code_ID_IF_2), .branches_zeros(branches_zero_if_id));
  jr_jalr jr_jalr_1 (.op_code(op_code_ID_IF_3), .jr_jalr(jr_jalr_if_id));
  R_TYPE r_type_1 (.op_code(op_code_EX_MEM), .r_type(R_TYPE_EX_MEM));
  I_TYPE i_type_1 (.op_code(op_code_EX_MEM_2), .i_type(I_TYPE_EX_MEM));
  JAL_JALR jal_jalr_1 (.op_code(op_code_EX_MEM_3), .jal_jalr(jal_jalr_ex_mem));
  or \or  (R_I_TYPE_EX_MEM, R_TYPE_EX_MEM, I_TYPE_EX_MEM);
  Comparator #(.width(3)) comparator_1 (.a(RD_IF_ID), .b(RD_EX_MEM), .eq(comparator_1_eq));  // open: gt, lt
  Comparator #(.width(3)) comparator_2 (.a(RD_IF_ID), .b(RD_EX_MEM), .eq(comparator_2_eq));  // open: gt, lt
  Comparator #(.width(3)) comparator_3 (.a(RD_IF_ID), .b(RD_EX_MEM), .eq(comparator_3_eq));  // open: gt, lt
  Comparator #(.width(3)) comparator_4 (.a(RD_IF_ID), .b(RD_EX_MEM), .eq(comparator_4_eq));  // open: gt, lt
  Comparator #(.width(3)) comparator_5 (.a(RD_IF_ID), .b(RD_EX_MEM), .eq(comparator_5_eq));  // open: gt, lt
  Comparator #(.width(3)) comparator_6 (.a(RD_IF_ID), .b(RD_EX_MEM), .eq(comparator_6_eq));  // open: gt, lt
  Comparator #(.width(3)) comparator_7 (.a(RD_IF_ID), .b(RD_EX_MEM), .eq(comparator_7_eq));  // open: gt, lt
  Comparator #(.width(3)) comparator_8 (.a(RD_IF_ID), .b(RD_EX_MEM), .eq(comparator_8_eq));  // open: gt, lt
  Comparator #(.width(3)) comparator_9 (.a(RD_IF_ID), .b(RD_EX_MEM), .eq(comparator_9_eq));  // open: gt, lt
  Comparator #(.width(3)) comparator_10 (.a(RD_IF_ID), .b(3'b111), .eq(comparator_10_eq));  // open: gt, lt
  Comparator #(.width(3)) comparator_11 (.a(RD_IF_ID), .b(3'b111), .eq(comparator_11_eq));  // open: gt, lt
  Comparator #(.width(3)) comparator_12 (.a(RD_IF_ID), .b(3'b111), .eq(comparator_12_eq));  // open: gt, lt
  and \and  (and_out, beq_bneif_id, comparator_1_eq);
  and and_2 (and_2_out, branches_zero_if_id, comparator_2_eq);
  and and_3 (and_3_out, jr_jalr_if_id, comparator_3_eq);
  and and_4 (and_4_out, beq_bneif_id, comparator_4_eq);
  and and_5 (and_5_out, branches_zero_if_id, comparator_5_eq);
  and and_6 (and_6_out, jr_jalr_if_id, comparator_6_eq);
  and and_7 (and_7_out, beq_bneif_id, comparator_7_eq);
  and and_8 (and_8_out, branches_zero_if_id, comparator_8_eq);
  and and_9 (and_9_out, jr_jalr_if_id, comparator_9_eq);
  and and_10 (and_10_out, beq_bneif_id, comparator_10_eq);
  and and_11 (and_11_out, branches_zero_if_id, comparator_11_eq);
  and and_12 (and_12_out, jr_jalr_if_id, comparator_12_eq);
  or or_2 (or_2_out, and_out, and_2_out, and_3_out);
  or or_3 (or_3_out, and_4_out, and_5_out, and_6_out);
  or or_4 (or_4_out, and_7_out, and_8_out, and_9_out);
  or or_5 (or_5_out, and_10_out, and_11_out, and_12_out);
  not not_1 (not_1_out, memory_read_ex_mem);
  and and_13 (alu_res_execution, R_I_TYPE_EX_MEM, or_2_out, register_write_EX_MEM, not_1_out);
  and and_14 (set_execution, set_EX_MEM, or_3_out, register_write_EX_MEM);
  and and_15 (sset_execution, sset_EX_MEM, or_4_out, register_write_EX_MEM);
  and and_16 (jal_jalr_execution, jal_jalr_ex_mem, or_5_out, register_write_EX_MEM);
  Multiplexer #(.width(3), .enable("false")) multiplexer_1 (
    .in0(3'b000), .in1(3'b001), .out(multiplexer_1_out), .sel(alu_res_execution));
  Multiplexer #(.width(3), .enable("false")) multiplexer_2 (
    .in0(multiplexer_1_out), .in1(3'b010), .out(multiplexer_2_out), .sel(sset_execution));
  Multiplexer #(.width(3), .enable("false")) multiplexer_3 (
    .in0(multiplexer_2_out), .in1(3'b011), .out(multiplexer_3_out), .sel(set_execution));
  Multiplexer #(.width(3), .enable("false")) multiplexer_4 (
    .in0(multiplexer_3_out), .in1(3'b100), .out(FWD_C), .sel(jal_jalr_execution));
endmodule

module forwarding_unit_decoding_stage_d (
  input  [4:0] op_code_ID_IF,
  input  [2:0] Rs_IF_ID,
  input  [2:0] RD_EX_MEM,
  input  [4:0] op_code_EX_MEM,
  input  [4:0] op_code_EX_MEM_2,
  input  [4:0] op_code_EX_MEM_3,
  input  register_write_EX_MEM,
  input  sset_EX_MEM,
  input  set_EX_MEM,
  input  memory_read_ex_mem,
  output [2:0] FWD_D
);

  wire alu_res_execution, and_2_out, and_3_out, and_4_out, and_out, beq_bneif_id, comparator_1_eq,
       comparator_2_eq, comparator_3_eq, comparator_4_eq, I_TYPE_EX_MEM, jal_jalr_ex_mem, jal_jalr_execution,
       not_1_out, R_I_TYPE_EX_MEM, R_TYPE_EX_MEM, set_execution, sset_execution;
  wire [2:0] multiplexer_1_out, multiplexer_2_out, multiplexer_3_out;

  beq_bne beq_bne_1 (.op_code(op_code_ID_IF), .beq_bne(beq_bneif_id));
  JAL_JALR jal_jalr_1 (.op_code(op_code_EX_MEM), .jal_jalr(jal_jalr_ex_mem));
  R_TYPE r_type_1 (.op_code(op_code_EX_MEM_2), .r_type(R_TYPE_EX_MEM));
  I_TYPE i_type_1 (.op_code(op_code_EX_MEM_3), .i_type(I_TYPE_EX_MEM));
  or \or  (R_I_TYPE_EX_MEM, R_TYPE_EX_MEM, I_TYPE_EX_MEM);
  Comparator #(.width(3)) comparator_1 (.a(Rs_IF_ID), .b(RD_EX_MEM), .eq(comparator_1_eq));  // open: gt, lt
  Comparator #(.width(3)) comparator_2 (.a(Rs_IF_ID), .b(RD_EX_MEM), .eq(comparator_2_eq));  // open: gt, lt
  Comparator #(.width(3)) comparator_3 (.a(Rs_IF_ID), .b(RD_EX_MEM), .eq(comparator_3_eq));  // open: gt, lt
  Comparator #(.width(3)) comparator_4 (.a(Rs_IF_ID), .b(3'b111), .eq(comparator_4_eq));  // open: gt, lt
  and \and  (and_out, beq_bneif_id, comparator_1_eq);
  and and_2 (and_2_out, beq_bneif_id, comparator_2_eq);
  and and_3 (and_3_out, beq_bneif_id, comparator_3_eq);
  and and_4 (and_4_out, beq_bneif_id, comparator_4_eq);
  not not_1 (not_1_out, memory_read_ex_mem);
  and and_5 (alu_res_execution, R_I_TYPE_EX_MEM, and_out, register_write_EX_MEM, not_1_out);
  and and_6 (set_execution, set_EX_MEM, and_2_out, register_write_EX_MEM);
  and and_7 (sset_execution, sset_EX_MEM, and_3_out, register_write_EX_MEM);
  and and_8 (jal_jalr_execution, jal_jalr_ex_mem, and_4_out, register_write_EX_MEM);
  Multiplexer #(.width(3), .enable("false")) multiplexer_1 (
    .in0(3'b000), .in1(3'b001), .out(multiplexer_1_out), .sel(alu_res_execution));
  Multiplexer #(.width(3), .enable("false")) multiplexer_2 (
    .in0(multiplexer_1_out), .in1(3'b010), .out(multiplexer_2_out), .sel(sset_execution));
  Multiplexer #(.width(3), .enable("false")) multiplexer_3 (
    .in0(multiplexer_2_out), .in1(3'b011), .out(multiplexer_3_out), .sel(set_execution));
  Multiplexer #(.width(3), .enable("false")) multiplexer_4 (
    .in0(multiplexer_3_out), .in1(3'b100), .out(FWD_D), .sel(jal_jalr_execution));
endmodule

module hazard_unit_part_1 (
  input  [2:0] RD_IF_ID,
  input  [2:0] RS_IF_ID,
  input  [2:0] RT_IF_ID,
  input  [2:0] RD_ID_EX,
  input  meory_read_ID_EX,
  input  sset_IF_ID,
  input  [4:0] op_code_IF_ID,
  input  [4:0] op_code_IF_ID_2,
  output stall_part_1
);

  wire and_2_out, and_3_out, and_out, comparator_1_eq, comparator_2_eq, comparator_3_eq, I_TYPE, or_2_out,
       or_out, R_TYPE;

  Comparator #(.width(3)) comparator_1 (.a(RS_IF_ID), .b(RD_ID_EX), .eq(comparator_1_eq));  // open: gt, lt
  Comparator #(.width(3)) comparator_2 (.a(RT_IF_ID), .b(RD_ID_EX), .eq(comparator_2_eq));  // open: gt, lt
  Comparator #(.width(3)) comparator_3 (.a(RD_IF_ID), .b(RD_ID_EX), .eq(comparator_3_eq));  // open: gt, lt
  R_TYPE r_type_1 (.op_code(op_code_IF_ID), .r_type(R_TYPE));
  I_TYPE i_type_1 (.op_code(op_code_IF_ID_2), .i_type(I_TYPE));
  and \and  (and_out, comparator_3_eq, sset_IF_ID);
  or \or  (or_out, comparator_1_eq, comparator_2_eq);
  and and_2 (and_2_out, or_out, R_TYPE);
  and and_3 (and_3_out, I_TYPE, comparator_1_eq);
  or or_2 (or_2_out, and_2_out, and_3_out, and_out);
  and and_4 (stall_part_1, or_2_out, meory_read_ID_EX);
endmodule

module hazard_unit_part_2 (
  input  [2:0] RS_IF_ID,
  input  [2:0] RD_EX_MEM,
  input  [2:0] RD_IF_ID,
  input  meory_read_EX_MEM,
  input  [4:0] op_code_IF_ID,
  input  [4:0] op_code_IF_ID_2,
  input  [4:0] op_code_IF_ID_3,
  input  [2:0] RD_ID_EX,
  input  meory_read_ID_EX,
  input  sset_ID_EX,
  input  set_ID_EX,
  input  [4:0] op_code_ID_EX,
  input  [4:0] op_code_ID_EX_2,
  input  [4:0] op_code_ID_EX_3,
  input  register_write_ID_EX,
  output stall_part_2
);

  wire and_2_out, and_3_out, and_4_out, and_5_out, and_6_out, and_7_out, and_8_out, and_9_out, and_10_out,
       and_out, beq_neq_if_id, branches_zeros_if_id, comparator_1_eq, comparator_2_eq, comparator_3_eq,
       comparator_4_eq, comparator_5_eq, comparator_6_eq, comparator_7_eq, comparator_8_eq, I_TYPE_ID_EX,
       jal_jalr_ID_EX, jr_jalr_if_id, or_2_out, or_3_out, or_out, R_TYPE_ID_EX;

  jr_jalr jr_jalr_1 (.op_code(op_code_IF_ID), .jr_jalr(jr_jalr_if_id));
  beq_bne beq_bne_1 (.op_code(op_code_IF_ID_2), .beq_bne(beq_neq_if_id));
  beranch_zero beranch_zero_1 (.op_code(op_code_IF_ID_3), .branches_zeros(branches_zeros_if_id));
  R_TYPE r_type_1 (.op_code(op_code_ID_EX), .r_type(R_TYPE_ID_EX));
  I_TYPE i_type_1 (.op_code(op_code_ID_EX_2), .i_type(I_TYPE_ID_EX));
  JAL_JALR jal_jalr_1 (.op_code(op_code_ID_EX_3), .jal_jalr(jal_jalr_ID_EX));
  Comparator #(.width(3)) comparator_1 (.a(RD_IF_ID), .b(RD_EX_MEM), .eq(comparator_1_eq));  // open: gt, lt
  Comparator #(.width(3)) comparator_2 (.a(RD_IF_ID), .b(RD_EX_MEM), .eq(comparator_2_eq));  // open: gt, lt
  Comparator #(.width(3)) comparator_3 (.a(RD_IF_ID), .b(RD_EX_MEM), .eq(comparator_3_eq));  // open: gt, lt
  Comparator #(.width(3)) comparator_4 (.a(RS_IF_ID), .b(RD_EX_MEM), .eq(comparator_4_eq));  // open: gt, lt
  Comparator #(.width(3)) comparator_5 (.a(RD_IF_ID), .b(RD_ID_EX), .eq(comparator_5_eq));  // open: gt, lt
  Comparator #(.width(3)) comparator_6 (.a(RD_IF_ID), .b(RD_ID_EX), .eq(comparator_6_eq));  // open: gt, lt
  Comparator #(.width(3)) comparator_7 (.a(RD_IF_ID), .b(RD_ID_EX), .eq(comparator_7_eq));  // open: gt, lt
  Comparator #(.width(3)) comparator_8 (.a(RS_IF_ID), .b(RD_ID_EX), .eq(comparator_8_eq));  // open: gt, lt
  and \and  (and_out, beq_neq_if_id, comparator_1_eq);
  and and_2 (and_2_out, jr_jalr_if_id, comparator_2_eq);
  and and_3 (and_3_out, branches_zeros_if_id, comparator_3_eq);
  and and_4 (and_4_out, beq_neq_if_id, comparator_4_eq);
  and and_5 (and_5_out, beq_neq_if_id, comparator_5_eq);
  and and_6 (and_6_out, jr_jalr_if_id, comparator_6_eq);
  and and_7 (and_7_out, branches_zeros_if_id, comparator_7_eq);
  and and_8 (and_8_out, beq_neq_if_id, comparator_8_eq);
  or \or  (or_out, and_out, and_2_out, and_3_out, and_4_out);
  or or_2 (or_2_out, and_5_out, and_6_out, and_7_out, and_8_out);
  or or_3 (or_3_out, meory_read_ID_EX, set_ID_EX, sset_ID_EX, R_TYPE_ID_EX, I_TYPE_ID_EX, jal_jalr_ID_EX);
  and and_9 (and_9_out, or_out, meory_read_EX_MEM);
  and and_10 (and_10_out, register_write_ID_EX, or_2_out, or_3_out);
  or or_4 (stall_part_2, and_9_out, and_10_out);
endmodule

module hazard_unit_part_3 (
  input  [2:0] RD_ID_EX,
  input  [2:0] RD_EX_MEM,
  input  [2:0] RD_IF_ID,
  input  [4:0] op_code_IF_ID,
  input  register_write_EX_MEM,
  input  register_write_ID_EX,
  output stall_part_3
);

  wire and_2_out, and_out, comparator_2_eq, comparator_3_eq, or_2_out, or_out, SW;

  Comparator #(.width(5)) comparator_1 (.a(op_code_IF_ID), .b(5'b10001), .eq(SW));  // open: gt, lt
  Comparator #(.width(3)) comparator_2 (.a(RD_IF_ID), .b(RD_EX_MEM), .eq(comparator_2_eq));  // open: gt, lt
  Comparator #(.width(3)) comparator_3 (.a(RD_IF_ID), .b(RD_ID_EX), .eq(comparator_3_eq));  // open: gt, lt
  and \and  (and_out, SW, comparator_2_eq);
  and and_2 (and_2_out, SW, comparator_3_eq);
  or \or  (or_out, and_out, and_2_out);
  or or_2 (or_2_out, register_write_EX_MEM, register_write_ID_EX);
  and and_3 (stall_part_3, or_out, or_2_out);
endmodule

module main_hazard_unit (
  input  hazard_unit_part_1,
  input  hazard_unit_part_2,
  input  hazard_unit_part_3,
  input  branches_taken,
  input  jr,
  input  jalr,
  input  j,
  input  jal,
  output stall_ID_EX__Disable_PC,
  output Stall_IF_ID
);

  or \or  (stall_ID_EX__Disable_PC, hazard_unit_part_1, hazard_unit_part_2, hazard_unit_part_3);
  or or_2 (Stall_IF_ID, branches_taken, jr, jalr, j, jal);
endmodule

module stall_support (
  input  stall,
  input  src_sel_1_IF_ID,
  input  jalr_IF_ID,
  input  reg_write_IF_ID,
  input  memory_read_IF_ID,
  input  memory_write_IF_ID,
  input  memory_to_register_IF_ID,
  input  alu_src_IF_ID,
  input  alu_op_0_IF_ID,
  input  alu_op_1_IF_ID,
  input  alu_op_2_IF_ID,
  input  alu_op_3_IF_ID,
  input  set_IF_ID,
  input  alu_op_4_IF_ID,
  input  sset_IF_ID,
  input  jump_IF_ID,
  input  src_sel_2_IF_ID,
  input  jal_IF_ID,
  input  _5_extend_sel_IF_ID,
  input  jr_IF_ID,
  input  sw_IF_ID,
  output src_sel_1_ID_EX,
  output jalr_ID_EX,
  output reg_write_ID_EX,
  output memory_read_ID_EX,
  output memory_write_ID_EX,
  output memory_to_register_ID_EX,
  output alu_src_ID_EX,
  output alu_op_0_ID_EX,
  output alu_op_1_ID_EX,
  output alu_op_2_ID_EX,
  output alu_op_3_ID_EX,
  output set_ID_EX,
  output alu_op_4_ID_EX,
  output sset_ID_EX,
  output jump_ID_EX,
  output src_sel_2_ID_EX,
  output jal_ID_EX,
  output _5_extend_sel_ID_EX,
  output jr_ID_EX,
  output swl_ID_EX
);

  Multiplexer #(.enable("false")) multiplexer_1 (.in0(src_sel_1_IF_ID), .in1(1'b0), .out(src_sel_1_ID_EX), .sel(stall));
  Multiplexer #(.enable("false")) multiplexer_2 (.in0(reg_write_IF_ID), .in1(1'b0), .out(reg_write_ID_EX), .sel(stall));
  Multiplexer #(.enable("false")) multiplexer_3 (
    .in0(memory_read_IF_ID), .in1(1'b0), .out(memory_read_ID_EX), .sel(stall));
  Multiplexer #(.enable("false")) multiplexer_4 (
    .in0(memory_write_IF_ID), .in1(1'b0), .out(memory_write_ID_EX), .sel(stall));
  Multiplexer #(.enable("false")) multiplexer_5 (
    .in0(memory_to_register_IF_ID), .in1(1'b0), .out(memory_to_register_ID_EX), .sel(stall));
  Multiplexer #(.enable("false")) multiplexer_6 (.in0(alu_src_IF_ID), .in1(1'b0), .out(alu_src_ID_EX), .sel(stall));
  Multiplexer #(.enable("false")) multiplexer_7 (.in0(alu_op_0_IF_ID), .in1(1'b0), .out(alu_op_0_ID_EX), .sel(stall));
  Multiplexer #(.enable("false")) multiplexer_8 (.in0(alu_op_1_IF_ID), .in1(1'b0), .out(alu_op_1_ID_EX), .sel(stall));
  Multiplexer #(.enable("false")) multiplexer_9 (.in0(alu_op_2_IF_ID), .in1(1'b0), .out(alu_op_2_ID_EX), .sel(stall));
  Multiplexer #(.enable("false")) multiplexer_10 (.in0(alu_op_3_IF_ID), .in1(1'b0), .out(alu_op_3_ID_EX), .sel(stall));
  Multiplexer #(.enable("false")) multiplexer_11 (.in0(alu_op_4_IF_ID), .in1(1'b0), .out(alu_op_4_ID_EX), .sel(stall));
  Multiplexer #(.enable("false")) multiplexer_12 (.in0(jump_IF_ID), .in1(1'b0), .out(jump_ID_EX), .sel(stall));
  Multiplexer #(.enable("false")) multiplexer_13 (.in0(jal_IF_ID), .in1(1'b0), .out(jal_ID_EX), .sel(stall));
  Multiplexer #(.enable("false")) multiplexer_14 (.in0(jr_IF_ID), .in1(1'b0), .out(jr_ID_EX), .sel(stall));
  Multiplexer #(.enable("false")) multiplexer_15 (.in0(jalr_IF_ID), .in1(1'b0), .out(jalr_ID_EX), .sel(stall));
  Multiplexer #(.enable("false")) multiplexer_16 (.in0(set_IF_ID), .in1(1'b0), .out(set_ID_EX), .sel(stall));
  Multiplexer #(.enable("false")) multiplexer_17 (.in0(sset_IF_ID), .in1(1'b0), .out(sset_ID_EX), .sel(stall));
  Multiplexer #(.enable("false")) multiplexer_18 (
    .in0(src_sel_2_IF_ID), .in1(1'b0), .out(src_sel_2_ID_EX), .sel(stall));
  Multiplexer #(.enable("false")) multiplexer_19 (
    .in0(_5_extend_sel_IF_ID), .in1(1'b0), .out(_5_extend_sel_ID_EX), .sel(stall));
  Multiplexer #(.enable("false")) multiplexer_20 (.in0(sw_IF_ID), .in1(1'b0), .out(swl_ID_EX), .sel(stall));
endmodule
