// Logisim project single cycle processor .circ as structural Verilog: 4 circuits, main circuit Register_File
module main (
  output zero_flag,
  output carry_out,
  output over_flow
);

  wire alu_src, and_2_out, and_out, beq, beqz, bgez, bgtz, blez, bltz, bne, bnez, branch_and_gate, clk,
       five_extend_sel, jal, jalr, jr, jump, memory_read, memory_to_register, memory_write, or_2_out,
       or_3_out, or_4_out, or_5_out, or_6_out, or_7_out, or_out, register_write, rest, set, source_sel_1,
       source_sel_2, sset, sw;
  wire [2:0] multiplexer_3_out, multiplexer_4_out, multiplexer_5_out, multiplexer_6_out;
  wire [4:0] _5_bits_immediate, alu_op, op_code;
  wire [7:5] _8_bits_immediate;
  wire [10:8] _11_bits_immediate;
  wire [17:0] bit_extender_9_out;
  wire [19:0] adder_1_out, adder_4_out, bit_extender_1_out, pc;
  wire [31:0] _5_bits_immediate_extended, _5_bits_immediate_sign_entended, _8_bits_immediate_sign_extended,
       _8_bits_immediate_sign_extended_shifted, _11_bits_immediate_sign_extended_, adder_2_out, adder_3_out,
       adder_5_out, alu_1_result, bit_extender_2_out, bit_extender_3_out, bit_extender_4_out,
       bit_extender_7_out, bit_extender_10_out, bit_extender_11_out, data_in_reg_file, multiplexer_1_out,
       multiplexer_2_out, multiplexer_7_out, multiplexer_8_out, multiplexer_9_out, multiplexer_11_out,
       multiplexer_12_out, multiplexer_13_out, multiplexer_14_out, ram_2_data, register_file_1_bus_a,
       register_file_1_bus_b;

  Multiplexer #(.width(32), .enable("false")) multiplexer_1 (
    .in0(multiplexer_2_out), .in1(alu_1_result), .out(multiplexer_1_out), .sel(or_out));
  Bit_Extender #(.in_width(32), .out_width(20)) bit_extender_1 (.in(multiplexer_1_out), .out(bit_extender_1_out));
  Clock u_clk (.out(clk));
  Counter #(.width(20), .max('hfffff)) u_PC (
    .load(1'b1), .D(bit_extender_1_out), .count(1'b0), .Q(pc), .clk(clk), .clr(rest));  // open: carry
  or \or  (or_out, jr, jalr);
  Adder #(.width(20)) adder_1 (.a(pc), .b(20'h1), .out(adder_1_out), .cin(1'b0));  // open: cout
  Button u_rest (.out(rest));
  RAM #(.addrWidth(20), .dataWidth(16)) ram_1 (
    .addr(pc), .data({op_code, _11_bits_immediate, _8_bits_immediate, _5_bits_immediate}), .sel(1'b1),
    .clk(clk), .ld(1'b1), .clr(rest));
  or or_2 (or_2_out, beqz, bltz, bgtz, bnez, bgez, blez);
  assign bit_extender_2_out = {{12{1'b0}}, adder_1_out};  // Bit_Extender bit_extender_2
  and \and  (and_out, or_2_out, branch_and_gate);
  control_unit control_unit_1 (
    .op_code(op_code), .source_sel_1(source_sel_1), .register_write(register_write),
    .memory_read(memory_read), .memory_write(memory_write), .memory_to_register(memory_to_register),
    .alu_src(alu_src), .alu_op_0(alu_op[0]), .alu_op_1(alu_op[1]), .alu_op_2(alu_op[2]),
    .alu_op_3(alu_op[3]), .alu_op_4(alu_op[4]), .jump(jump), .jal(jal), .jr(jr), .jalr(jalr), .BEQ(beq),
    .BNE(bne), .BEQZ(beqz), .BNEZ(bnez), .BLTZ(bltz), .BGEZ(bgez), .BGTZ(bgtz), .BLEZ(blez), .SET(set),
    .SSET(sset), .source_sel_2(source_sel_2), .five_extend_sel(five_extend_sel), .SW(sw));
  Multiplexer #(.width(32), .enable("false")) multiplexer_2 (
    .in0(multiplexer_7_out), .in1(adder_2_out), .out(multiplexer_2_out), .sel(and_out));
  assign bit_extender_3_out = {{12{1'b0}}, pc};  // Bit_Extender bit_extender_3
  Adder #(.width(32)) adder_2 (
    .a(bit_extender_3_out), .b(_8_bits_immediate_sign_extended), .out(adder_2_out), .cin(1'b0));  // open: cout
  Multiplexer #(.width(3), .enable("false")) multiplexer_3 (
    .in0(_5_bits_immediate[4:2]), .in1(_8_bits_immediate), .out(multiplexer_3_out), .sel(source_sel_1));
  Multiplexer #(.width(3), .enable("false")) multiplexer_4 (
    .in0(multiplexer_3_out), .in1(_11_bits_immediate), .out(multiplexer_4_out), .sel(source_sel_2));
  Multiplexer #(.width(3), .enable("false")) multiplexer_5 (
    .in0(_8_bits_immediate), .in1(_11_bits_immediate), .out(multiplexer_5_out), .sel(sw));
  Multiplexer #(.width(3), .enable("false")) multiplexer_6 (
    .in0(_11_bits_immediate), .in1(3'b111), .out(multiplexer_6_out), .sel(or_3_out));
  or or_3 (or_3_out, jal, jalr);
  Register_File register_file_1 (
    .Data_in(data_in_reg_file), .BUS_A(register_file_1_bus_a), .BUS_B(register_file_1_bus_b),
    .Register_write(register_write), .reg_destination(multiplexer_6_out), .CLK(clk), .REST(rest),
    .register_read_1(multiplexer_4_out), .register_read_2(multiplexer_5_out));
  assign bit_extender_4_out = {{12{1'b0}}, pc};  // Bit_Extender bit_extender_4
  Multiplexer #(.width(32), .enable("false")) multiplexer_7 (
    .in0(multiplexer_11_out), .in1(adder_3_out), .out(multiplexer_7_out), .sel(and_2_out));
  Multiplexer #(.width(32), .enable("false")) multiplexer_8 (
    .in0(register_file_1_bus_b), .in1(_5_bits_immediate_extended), .out(multiplexer_8_out), .sel(alu_src));
  assign _11_bits_immediate_sign_extended_ = {{21{_11_bits_immediate[10]}}, {_11_bits_immediate, _8_bits_immediate, _5_bits_immediate}};  // Bit_Extender bit_extender_5
  assign _8_bits_immediate_sign_extended = {{24{_8_bits_immediate[7]}}, {_8_bits_immediate, _5_bits_immediate}};  // Bit_Extender bit_extender_6
  assign bit_extender_7_out = {{27{1'b0}}, _5_bits_immediate};  // Bit_Extender bit_extender_7
  assign _5_bits_immediate_sign_entended = {{27{_5_bits_immediate[4]}}, _5_bits_immediate};  // Bit_Extender bit_extender_8
  Adder #(.width(32)) adder_3 (
    .a(bit_extender_4_out), .b(_5_bits_immediate_sign_entended), .out(adder_3_out));  // open: cin, cout
  Multiplexer #(.width(32), .enable("false")) multiplexer_9 (
    .in0(multiplexer_8_out), .in1(_8_bits_immediate_sign_extended), .out(multiplexer_9_out), .sel(or_4_out));
  or or_4 (or_4_out, jr, jalr);
  Shifter #(.width(32)) shifter_1 (
    .in(_8_bits_immediate_sign_extended), .\dist (5'b00001), .out(_8_bits_immediate_sign_extended_shifted));
  Multiplexer #(.width(32), .enable("false")) multiplexer_10 (
    .in0(bit_extender_7_out), .in1(_5_bits_immediate_sign_entended), .out(_5_bits_immediate_extended),
    .sel(five_extend_sel));
  and and_2 (and_2_out, or_5_out, branch_and_gate);
  or or_5 (or_5_out, beq, bne);
  ALU alu_1 (
    .A(register_file_1_bus_a), .B(multiplexer_9_out), .ALU_OP(alu_op), .fun(_5_bits_immediate[1:0]),
    .branch(branch_and_gate), .result(alu_1_result), .zero_flag(zero_flag), .carry_out(carry_out),
    .over_flow(over_flow));
  Multiplexer #(.width(32), .enable("false")) multiplexer_11 (
    .in0(bit_extender_2_out), .in1(adder_5_out), .out(multiplexer_11_out), .sel(or_6_out));
  or or_6 (or_6_out, jump, jal);
  Bit_Extender #(.in_width(32), .out_width(18), .\type ("sign")) bit_extender_9 (
    .in(alu_1_result), .out(bit_extender_9_out));
  RAM #(.addrWidth(18), .dataWidth(32), .bus("separate")) ram_2 (
    .addr(bit_extender_9_out), .din(register_file_1_bus_b), .data(ram_2_data), .str(memory_write),
    .sel(1'b1), .clk(clk), .ld(memory_read), .clr(rest));
  Adder #(.width(20)) adder_4 (.a(pc), .b(20'h1), .out(adder_4_out), .cin(1'b0));  // open: cout
  assign bit_extender_10_out = {{12{1'b0}}, pc};  // Bit_Extender bit_extender_10
  assign bit_extender_11_out = {{12{adder_4_out[19]}}, adder_4_out};  // Bit_Extender bit_extender_11
  Adder #(.width(32)) adder_5 (
    .a(bit_extender_10_out), .b(_11_bits_immediate_sign_extended_), .out(adder_5_out), .cin(1'b0));  // open: cout
  Multiplexer #(.width(32), .enable("false")) multiplexer_12 (
    .in0(alu_1_result), .in1(ram_2_data), .out(multiplexer_12_out), .sel(memory_to_register));
  Multiplexer #(.width(32), .enable("false")) multiplexer_13 (
    .in0(multiplexer_12_out), .in1(_8_bits_immediate_sign_extended), .out(multiplexer_13_out), .sel(set));
  Multiplexer #(.width(32), .enable("false")) multiplexer_14 (
    .in0(multiplexer_13_out), .in1({alu_1_result[31:8], _8_bits_immediate, _5_bits_immediate}),
    .out(multiplexer_14_out), .sel(sset));
  Multiplexer #(.width(32), .enable("false")) multiplexer_15 (
    .in0(multiplexer_14_out), .in1(bit_extender_11_out), .out(data_in_reg_file), .sel(or_7_out));
  or or_7 (or_7_out, jal, jalr);

  // Other names for the same wires on the sheet: _8_bits_immediate[4:0] = _5_bits_immediate;
  //   _11_bits_immediate[7:0] = {_8_bits_immediate, _5_bits_immediate}; function_field[1:0] = _5_bits_immediate[1:0]

  // Notes on the sheet:
  //   stage1
  //   pc+1
  //   control unit
  //   mux_b
  //   branches#zero_target_address
  //   2:4
  //   5:7
  //   8:10
  //   stage2
  //   source_sel_1
  //   source_sel_2
  //   sw
  //   destenation_sel
  //   stage3
  //   mux_a
  //   alu_first_operand
  //   alu_src_mux_1
  //   branches_target_address
  //   alu_src
  //   alu_src_mux_2
  //   shifted_immediate
  //   branchs
  //   alu_result
  //   stage4
  //   mux_c
  //   jump_target_address
  //   jal#jalr
  //   memory_to_register
  //   set
  //   sset
  //   stage5
endmodule

module Register_File (
  input  Register_write,
  input  [2:0] register_read_1,
  input  [2:0] register_read_2,
  input  [2:0] reg_destination,
  input  CLK,
  input  REST,
  input  [31:0] Data_in,
  output [31:0] BUS_A,
  output [31:0] BUS_B
);

  wire decoder_1_out0, decoder_1_out1, decoder_1_out2, decoder_1_out3, decoder_1_out4, decoder_1_out5,
       decoder_1_out6, decoder_1_out7;
  wire [31:0] R0_q, R1_q, R2_q, R3_q, R4_q, R5_q, R6_q, R7_q;

  Decoder #(.select(3), .disabled(0)) decoder_1 (
    .out0(decoder_1_out0), .out1(decoder_1_out1), .out2(decoder_1_out2), .out3(decoder_1_out3),
    .out4(decoder_1_out4), .out5(decoder_1_out5), .out6(decoder_1_out6), .out7(decoder_1_out7),
    .sel(reg_destination), .en(Register_write));
  Register #(.width(32)) R0 (.D(Data_in), .en(decoder_1_out0), .Q(R0_q), .clk(CLK), .clr(REST));
  Register #(.width(32)) R1 (.D(Data_in), .en(decoder_1_out1), .Q(R1_q), .clk(CLK), .clr(REST));
  Register #(.width(32)) R2 (.D(Data_in), .en(decoder_1_out2), .Q(R2_q), .clk(CLK), .clr(REST));
  Register #(.width(32)) R3 (.D(Data_in), .en(decoder_1_out3), .Q(R3_q), .clk(CLK), .clr(REST));
  Register #(.width(32)) R4 (.D(Data_in), .en(decoder_1_out4), .Q(R4_q), .clk(CLK), .clr(REST));
  Register #(.width(32)) R5 (.D(Data_in), .en(decoder_1_out5), .Q(R5_q), .clk(CLK), .clr(REST));
  Register #(.width(32)) R6 (.D(Data_in), .en(decoder_1_out6), .Q(R6_q), .clk(CLK), .clr(REST));
  Register #(.width(32)) R7 (.D(Data_in), .en(decoder_1_out7), .Q(R7_q), .clk(CLK), .clr(REST));
  Multiplexer #(.select(3), .width(32), .enable("false")) multiplexer_1 (
    .in0(R0_q), .in1(R1_q), .in2(R2_q), .in3(R3_q), .in4(R4_q), .in5(R5_q), .in6(R6_q), .in7(R7_q),
    .out(BUS_A), .sel(register_read_1));
  Multiplexer #(.select(3), .width(32), .enable("false")) multiplexer_2 (
    .in0(R0_q), .in1(R1_q), .in2(R2_q), .in3(R3_q), .in4(R4_q), .in5(R5_q), .in6(R6_q), .in7(R7_q),
    .out(BUS_B), .sel(register_read_2));
endmodule

module ALU (
  input  [31:0] A,
  input  [31:0] B,
  input  [4:0] ALU_OP,
  input  [1:0] fun,
  output branch,
  output [31:0] result,
  output zero_flag,
  output carry_out,
  output over_flow
);

  wire and_2_out, and_3_out, bit_extender_14_out, bit_extender_15_out, carry_out_t, carry_out_t_t,
       comparator_1_lt, comparator_2_eq, comparator_3_eq, comparator_4_eq, comparator_5_eq, comparator_6_eq,
       comparator_7_lt, comparator_8_eq, comparator_8_gt, comparator_9_gt, comparator_10_eq,
       comparator_10_lt, multiplexer_3_out, multiplexer_4_out, not_2_out, not_3_out, or_2_out, or_3_out,
       xor_3_out, xor_4_out, xor_5_out, xor_6_out;
  wire [4:0] bit_extender_1_out, bit_extender_2_out, bit_extender_3_out;
  wire [31:0] and_out, bit_extender_4_out, bit_extender_5_out, bit_extender_6_out, bit_extender_7_out,
       bit_extender_8_out, bit_extender_9_out, bit_extender_10_out, bit_extender_11_out, bit_extender_12_out,
       bit_extender_13_out, multiplexer_1_out, multiplexer_2_out, not_1_out, or_out, shifter_1_out,
       shifter_2_out, shifter_3_out, shifter_4_out, tunnel, tunnel_t, xor_2_out, xor_out;

  Bit_Extender #(.in_width(32), .out_width(5)) bit_extender_1 (.in(B), .out(bit_extender_1_out));
  Bit_Extender #(.in_width(32), .out_width(5)) bit_extender_2 (.in(B), .out(bit_extender_2_out));
  Bit_Extender #(.in_width(32), .out_width(5)) bit_extender_3 (.in(B), .out(bit_extender_3_out));
  Adder #(.width(32)) adder_1 (.a(A), .b(B), .out(tunnel), .cin(1'b0), .cout(carry_out_t));
  Subtractor #(.width(32)) subtractor_1 (.a(B), .b(A), .out(tunnel_t), .bin(1'b0), .bout(carry_out_t_t));
  Comparator #(.width(32)) comparator_1 (.a(B), .b(A), .lt(comparator_1_lt));  // open: gt, eq
  Comparator #(.width(32)) comparator_2 (.a(A), .b(B), .eq(comparator_2_eq));  // open: gt, lt
  Shifter #(.width(32)) shifter_1 (.in(A), .\dist (bit_extender_1_out), .out(shifter_1_out));
  Shifter #(.width(32), .shift("lr")) shifter_2 (.in(A), .\dist (bit_extender_2_out), .out(shifter_2_out));
  Shifter #(.width(32), .shift("rl")) shifter_3 (.in(A), .\dist (bit_extender_3_out), .out(shifter_3_out));
  Comparator #(.width(32)) comparator_3 (.a(A), .b(B), .eq(comparator_3_eq));  // open: gt, lt
  Comparator #(.width(32)) comparator_4 (.a(A), .b(B), .eq(comparator_4_eq));  // open: gt, lt
  Comparator #(.width(32)) comparator_5 (.a(A), .b({32{1'b0}}), .eq(comparator_5_eq));  // open: gt, lt
  Comparator #(.width(32)) comparator_6 (.a(A), .b({32{1'b0}}), .eq(comparator_6_eq));  // open: gt, lt
  Comparator #(.width(32)) comparator_7 (.a(A), .b({32{1'b0}}), .lt(comparator_7_lt));  // open: gt, eq
  Comparator #(.width(32)) comparator_8 (
    .a(A), .b({32{1'b0}}), .gt(comparator_8_gt), .eq(comparator_8_eq));  // open: lt
  Comparator #(.width(32)) comparator_9 (.a(A), .b({32{1'b0}}), .gt(comparator_9_gt));  // open: eq, lt
  Comparator #(.width(32)) comparator_10 (
    .a(A), .b({32{1'b0}}), .eq(comparator_10_eq), .lt(comparator_10_lt));  // open: gt
  Shifter #(.width(32)) shifter_4 (.in(A), .\dist (5'b01000), .out(shifter_4_out));
  assign and_out = A & B;  // AND_Gate and, 32 bits wide
  assign or_out = A | B;  // OR_Gate or, 32 bits wide
  assign xor_out = A ^ B;  // XOR_Gate xor, 32 bits wide
  assign not_1_out = ~xor_2_out;  // NOT_Gate not_1, 32 bits wide
  assign xor_2_out = A ^ B;  // XOR_Gate xor_2, 32 bits wide
  assign bit_extender_4_out = {{31{1'b0}}, comparator_3_eq};  // Bit_Extender bit_extender_4
  not not_2 (not_2_out, comparator_6_eq);
  or or_2 (or_2_out, comparator_8_gt, comparator_8_eq);
  not not_3 (not_3_out, comparator_4_eq);
  assign bit_extender_5_out = {{31{1'b0}}, not_3_out};  // Bit_Extender bit_extender_5
  assign bit_extender_6_out = {{31{1'b0}}, comparator_5_eq};  // Bit_Extender bit_extender_6
  assign bit_extender_7_out = {{31{1'b0}}, not_2_out};  // Bit_Extender bit_extender_7
  assign bit_extender_8_out = {{31{1'b0}}, comparator_7_lt};  // Bit_Extender bit_extender_8
  assign bit_extender_9_out = {{31{1'b0}}, comparator_9_gt};  // Bit_Extender bit_extender_9
  or or_3 (or_3_out, comparator_10_eq, comparator_10_lt);
  assign bit_extender_10_out = {{31{1'b0}}, or_3_out};  // Bit_Extender bit_extender_10
  assign bit_extender_11_out = {{31{1'b0}}, comparator_1_lt};  // Bit_Extender bit_extender_11
  assign bit_extender_12_out = {{31{1'b0}}, comparator_2_eq};  // Bit_Extender bit_extender_12
  assign bit_extender_13_out = {{31{1'b0}}, or_2_out};  // Bit_Extender bit_extender_13
  Multiplexer #(.select(2), .width(32), .enable("false")) multiplexer_1 (
    .in0(and_out), .in1(or_out), .in2(xor_out), .in3(not_1_out), .out(multiplexer_1_out), .sel(fun));
  Multiplexer #(.select(2), .width(32), .enable("false")) multiplexer_2 (
    .in0(tunnel), .in1(tunnel_t), .in2(bit_extender_11_out), .in3(bit_extender_12_out),
    .out(multiplexer_2_out), .sel(fun));
  xor xor_3 (xor_3_out, A[31], tunnel[31]);
  xor xor_4 (xor_4_out, tunnel[31], B[31]);
  xor xor_5 (xor_5_out, A[31], tunnel_t[31]);
  xor xor_6 (xor_6_out, tunnel_t[31], ~B[31]);  // XOR_Gate
  and and_2 (and_2_out, xor_3_out, xor_4_out);
  and and_3 (and_3_out, xor_5_out, xor_6_out);
  Bit_Extender #(.in_width(2), .out_width(1)) bit_extender_14 (.in(fun), .out(bit_extender_14_out));
  Multiplexer #(.enable("false")) multiplexer_3 (
    .in0(carry_out_t), .in1(carry_out_t_t), .out(multiplexer_3_out), .sel(bit_extender_14_out));
  Bit_Extender #(.in_width(2), .out_width(1)) bit_extender_15 (.in(fun), .out(bit_extender_15_out));
  Multiplexer #(.enable("false")) multiplexer_4 (
    .in0(and_2_out), .in1(and_3_out), .out(multiplexer_4_out), .sel(bit_extender_15_out));
  Multiplexer #(.select(5), .width(32), .enable("false")) multiplexer_5 (
    .in0(multiplexer_1_out), .in1(multiplexer_2_out), .in2(and_out), .in3(or_out), .in4(xor_out),
    .in5(not_1_out), .in6(tunnel), .in7(bit_extender_11_out), .in8(bit_extender_12_out), .in9(shifter_1_out),
    .in10(shifter_2_out), .in11(shifter_3_out), .in12(bit_extender_4_out), .in13(bit_extender_5_out),
    .in14(tunnel), .in15(tunnel), .in16(bit_extender_6_out), .in17(bit_extender_7_out),
    .in18(bit_extender_8_out), .in19(bit_extender_13_out), .in20(bit_extender_9_out),
    .in21(bit_extender_10_out), .in22(tunnel), .in23(tunnel), .in24(shifter_4_out), .in25({32{1'b0}}),
    .in26({32{1'b0}}), .in27({32{1'b0}}), .in28({32{1'b0}}), .in29({32{1'b0}}), .in30({32{1'b0}}),
    .in31({32{1'b0}}), .out({result[31:1], branch}), .sel(ALU_OP));
  Multiplexer #(.select(5), .enable("false")) multiplexer_6 (
    .in0(1'b0), .in1(multiplexer_3_out), .in2(1'b0), .in3(1'b0), .in4(1'b0), .in5(1'b0), .in6(carry_out_t),
    .in7(1'b0), .in8(1'b0), .in9(1'b0), .in10(1'b0), .in11(1'b0), .in12(1'b0), .in13(1'b0), .in14(1'b0),
    .in15(1'b0), .in16(1'b0), .in17(1'b0), .in18(1'b0), .in19(1'b0), .in20(1'b0), .in21(1'b0), .in22(1'b0),
    .in23(1'b0), .in24(1'b0), .in25(1'b0), .in26(1'b0), .in27(1'b0), .in28(1'b0), .in29(1'b0), .in30(1'b0),
    .in31(1'b0), .out(carry_out), .sel(ALU_OP));
  Multiplexer #(.select(5), .enable("false")) multiplexer_7 (
    .in0(1'b0), .in1(multiplexer_4_out), .in2(1'b0), .in3(1'b0), .in4(1'b0), .in5(1'b0), .in6(and_2_out),
    .in7(1'b0), .in8(1'b0), .in9(1'b0), .in10(1'b0), .in11(1'b0), .in12(1'b0), .in13(1'b0), .in14(1'b0),
    .in15(1'b0), .in16(1'b0), .in17(1'b0), .in18(1'b0), .in19(1'b0), .in20(1'b0), .in21(1'b0), .in22(1'b0),
    .in23(1'b0), .in24(1'b0), .in25(1'b0), .in26(1'b0), .in27(1'b0), .in28(1'b0), .in29(1'b0), .in30(1'b0),
    .in31(1'b0), .out(over_flow), .sel(ALU_OP));
  Comparator #(.width(32)) comparator_11 (.a({result[31:1], branch}), .b({32{1'b0}}), .eq(zero_flag));  // open: gt, lt

  assign result[0] = branch;

  // Notes on the sheet:
  //   slt
  //   seq
  //   sll
  //   srl
  //   ROR
endmodule

module control_unit (
  input  [4:0] op_code,
  output source_sel_1,
  output register_write,
  output memory_read,
  output memory_write,
  output memory_to_register,
  output alu_src,
  output alu_op_0,
  output alu_op_1,
  output alu_op_2,
  output alu_op_3,
  output alu_op_4,
  output jump,
  output jal,
  output jr,
  output jalr,
  output BEQ,
  output BNE,
  output BEQZ,
  output BNEZ,
  output BLTZ,
  output BGEZ,
  output BGTZ,
  output BLEZ,
  output SET,
  output SSET,
  output source_sel_2,
  output five_extend_sel,
  output SW
);

  Multiplexer #(.select(5), .width(28), .enable("false")) multiplexer_1 (
    .in0(28'h2), .in1(28'h42), .in2({28{1'b0}}), .in3({28{1'b0}}), .in4(28'ha3), .in5(28'he3), .in6(28'h123),
    .in7(28'h163), .in8(28'h40001a3), .in9(28'h40001e3), .in10(28'h4000223), .in11(28'h263), .in12(28'h2a3),
    .in13(28'h2e3), .in14(28'h6008300), .in15(28'h6010340), .in16(28'h40003b7), .in17(28'hc0003e9),
    .in18({28{1'b0}}), .in19({28{1'b0}}), .in20(28'h2020400), .in21(28'h2040440), .in22(28'h2080480),
    .in23(28'h21004c0), .in24(28'h2200500), .in25(28'h2400540), .in26(28'h2002580), .in27(28'h20045c2),
    .in28(28'h800002), .in29(28'h3000602), .in30(28'h800), .in31(28'h1002),
    .out({SW, five_extend_sel, source_sel_2, SSET, SET, BLEZ, BGTZ, BGEZ, BLTZ, BNEZ, BEQZ, BNE, BEQ, jalr, jr, jal, jump, alu_op_4, alu_op_3, alu_op_2, alu_op_1, alu_op_0, alu_src, memory_to_register, memory_write, memory_read, register_write, source_sel_1}),
    .sel(op_code));
endmodule
